// Logisim project 16-Single_Cycle_CPU.circ as structural Verilog
module _1_bit_Logic_unit (
  input  A,
  input  B,
  input  [1:0] S1S0,
  output Result
);

  wire and_1_out, not_1_out, or_1_out, xor_1_out;

  and and_1 (and_1_out, A, B);
  or or_1 (or_1_out, A, B);
  xor xor_1 (xor_1_out, A, B);
  not not_1 (not_1_out, A);
  Multiplexer #(.select(2), .enable("false")) multiplexer_1 (
    .in0(and_1_out), .in1(or_1_out), .in2(xor_1_out), .in3(not_1_out), .out(Result), .sel(S1S0));
endmodule

module _2_bit_logic_unit (
  input  A0,
  input  B0,
  input  A1,
  input  B1,
  input  [1:0] S1S0,
  output S0,
  output S1
);

  wire and_1_out, and_2_out, not_1_out, not_2_out, or_1_out, or_2_out, xor_1_out, xor_2_out;

  and and_1 (and_1_out, A0, B0);
  or or_1 (or_1_out, A0, B0);
  xor xor_1 (xor_1_out, A0, B0);
  not not_1 (not_1_out, A0);
  and and_2 (and_2_out, A1, B1);
  or or_2 (or_2_out, A1, B1);
  xor xor_2 (xor_2_out, A1, B1);
  not not_2 (not_2_out, A1);
  Multiplexer #(.select(2), .enable("false")) multiplexer_1 (
    .in0(and_1_out), .in1(or_1_out), .in2(xor_1_out), .in3(not_1_out), .out(S0), .sel(S1S0));
  Multiplexer #(.select(2), .enable("false")) multiplexer_2 (
    .in0(and_2_out), .in1(or_2_out), .in2(xor_2_out), .in3(not_2_out), .out(S1), .sel(S1S0));
endmodule

module _2_bit_LU (
  input  [1:0] A,
  input  [1:0] B,
  input  [1:0] S1S0,
  output [1:0] Result
);

  _1_bit_Logic_unit u_1_bit_logic_unit_1 (.A(A[0]), .B(B[0]), .S1S0(S1S0), .Result(Result[0]));
  _1_bit_Logic_unit u_1_bit_logic_unit_2 (.A(A[1]), .B(B[1]), .S1S0(S1S0), .Result(Result[1]));
endmodule

module _4_bit_LU (
  input  [3:0] A,
  input  [3:0] B,
  input  [1:0] S1S0,
  output [3:0] Result
);

  _1_bit_Logic_unit u_1_bit_logic_unit_1 (.A(A[0]), .B(B[0]), .S1S0(S1S0), .Result(Result[0]));
  _1_bit_Logic_unit u_1_bit_logic_unit_2 (.A(A[1]), .B(B[1]), .S1S0(S1S0), .Result(Result[1]));
  _1_bit_Logic_unit u_1_bit_logic_unit_3 (.A(A[2]), .B(B[2]), .S1S0(S1S0), .Result(Result[2]));
  _1_bit_Logic_unit u_1_bit_logic_unit_4 (.A(A[3]), .B(B[3]), .S1S0(S1S0), .Result(Result[3]));
endmodule

module _1_bit_Adder (
  input  A,
  input  B,
  input  Cin,
  output S,
  output Cout
);

  wire and_1_out, and_2_out, xor_1_out;

  xor xor_1 (xor_1_out, A, B);
  and and_1 (and_1_out, Cin, xor_1_out);
  and and_2 (and_2_out, B, A);
  xor xor_2 (S, xor_1_out, Cin);
  or or_1 (Cout, and_1_out, and_2_out);
endmodule

module _1_bit_Arithmetic_Unit (
  input  Cin,
  input  A,
  input  B,
  input  [1:0] S1S0,
  input  Const,
  output Sum,
  output Count
);

  wire multiplexer_1_out, not_1_out, not_2_out;

  not not_1 (not_1_out, B);
  not not_2 (not_2_out, Const);
  Multiplexer #(.select(2), .enable("false")) multiplexer_1 (
    .in0(B), .in1(not_1_out), .in2(Const), .in3(not_2_out), .out(multiplexer_1_out), .sel(S1S0));
  _1_bit_Adder u_1_bit_adder_1 (.B(multiplexer_1_out), .Cin(Cin), .S(Sum), .Cout(Count), .A(A));
endmodule

module _4_bit_Arithmetic_Unit (
  input  A3,
  input  A2,
  input  A1,
  input  A0,
  input  B3,
  input  B2,
  input  B1,
  input  B0,
  input  [1:0] S1S0,
  input  Cin,
  output Cout,
  output S3,
  output S2,
  output S1,
  output S0
);

  wire n1_bit_arithmetic_unit_1_count, n1_bit_arithmetic_unit_2_count, n1_bit_arithmetic_unit_3_count;

  _1_bit_Arithmetic_Unit u_1_bit_arithmetic_unit_1 (
    .Cin(Cin), .A(A0), .B(B0), .S1S0(S1S0), .Sum(S0), .Count(n1_bit_arithmetic_unit_1_count), .Const(1'b0));
  _1_bit_Arithmetic_Unit u_1_bit_arithmetic_unit_2 (
    .Cin(n1_bit_arithmetic_unit_1_count), .A(A1), .B(B1), .S1S0(S1S0), .Sum(S1),
    .Count(n1_bit_arithmetic_unit_2_count), .Const(1'b0));
  _1_bit_Arithmetic_Unit u_1_bit_arithmetic_unit_3 (
    .Cin(n1_bit_arithmetic_unit_2_count), .A(A2), .B(B2), .S1S0(S1S0), .Sum(S2),
    .Count(n1_bit_arithmetic_unit_3_count), .Const(1'b0));
  _1_bit_Arithmetic_Unit u_1_bit_arithmetic_unit_4 (
    .Cin(n1_bit_arithmetic_unit_3_count), .A(A3), .B(B3), .S1S0(S1S0), .Sum(S3), .Count(Cout), .Const(1'b0));
endmodule

module _16_bit_Arithmetic_Unit (
  input  [1:0] S1S0,
  input  Cin,
  input  A15,
  input  A14,
  input  A13,
  input  A12,
  input  A11,
  input  A10,
  input  A9,
  input  A8,
  input  A7,
  input  A6,
  input  A5,
  input  A4,
  input  A3,
  input  A2,
  input  A1,
  input  A0,
  input  B15,
  input  B14,
  input  B13,
  input  B12,
  input  B11,
  input  B10,
  input  B9,
  input  B8,
  input  B7,
  input  B6,
  input  B5,
  input  B4,
  input  B3,
  input  B2,
  input  B1,
  input  B0,
  output Cout,
  output S15,
  output S14,
  output S13,
  output S12,
  output S11,
  output S10,
  output S9,
  output S8,
  output S7,
  output S6,
  output S5,
  output S4,
  output S3,
  output S2,
  output S1,
  output S0
);

  wire n4_bit_arithmetic_unit_1_cout, n4_bit_arithmetic_unit_2_cout, n4_bit_arithmetic_unit_3_cout;

  _4_bit_Arithmetic_Unit u_4_bit_arithmetic_unit_1 (
    .Cin(Cin), .S1S0(S1S0), .Cout(n4_bit_arithmetic_unit_1_cout), .A3(A3), .A2(A2), .A1(A1), .A0(A0),
    .B3(B3), .B2(B2), .B1(B1), .B0(B0), .S3(S3), .S2(S2), .S1(S1), .S0(S0));
  _4_bit_Arithmetic_Unit u_4_bit_arithmetic_unit_2 (
    .Cin(n4_bit_arithmetic_unit_1_cout), .S1S0(S1S0), .Cout(n4_bit_arithmetic_unit_2_cout), .A3(A7), .A2(A6),
    .A1(A5), .A0(A4), .B3(B7), .B2(B6), .B1(B5), .B0(B4), .S3(S7), .S2(S6), .S1(S5), .S0(S4));
  _4_bit_Arithmetic_Unit u_4_bit_arithmetic_unit_3 (
    .Cin(n4_bit_arithmetic_unit_2_cout), .S1S0(S1S0), .Cout(n4_bit_arithmetic_unit_3_cout), .A3(A11),
    .A2(A10), .A1(A9), .A0(A8), .B3(B11), .B2(B10), .B1(B9), .B0(B8), .S3(S11), .S2(S10), .S1(S9), .S0(S8));
  _4_bit_Arithmetic_Unit u_4_bit_arithmetic_unit_4 (
    .Cin(n4_bit_arithmetic_unit_3_cout), .S1S0(S1S0), .Cout(Cout), .A3(A15), .A2(A14), .A1(A13), .A0(A12),
    .B3(B15), .B2(B14), .B1(B13), .B0(B12), .S3(S15), .S2(S14), .S1(S13), .S0(S12));
endmodule

module _4_bit_Adder (
  input  A3,
  input  A2,
  input  A1,
  input  A0,
  input  B3,
  input  B2,
  input  B1,
  input  B0,
  input  Cin,
  output S3,
  output S2,
  output S1,
  output S0,
  output Cout
);

  wire n1_bit_adder_1_cout, n1_bit_adder_2_cout, n1_bit_adder_3_cout;

  _1_bit_Adder u_1_bit_adder_1 (.B(B0), .Cin(Cin), .S(S0), .Cout(n1_bit_adder_1_cout), .A(A0));
  _1_bit_Adder u_1_bit_adder_2 (.B(B1), .Cin(n1_bit_adder_1_cout), .S(S1), .Cout(n1_bit_adder_2_cout), .A(A1));
  _1_bit_Adder u_1_bit_adder_3 (.B(B2), .Cin(n1_bit_adder_2_cout), .S(S2), .Cout(n1_bit_adder_3_cout), .A(A2));
  _1_bit_Adder u_1_bit_adder_4 (.B(B3), .Cin(n1_bit_adder_3_cout), .S(S3), .Cout(Cout), .A(A3));
endmodule

module _4_bit_Multiplier (
  input  Cin,
  input  A4,
  input  A3,
  input  A2,
  input  A1,
  input  B4,
  input  B3,
  input  B2,
  input  B1,
  output S8,
  output S7,
  output S6,
  output S5,
  output S4,
  output S3,
  output S2,
  output S1
);

  wire and_2_out, and_3_out, and_4_out, and_5_out, and_6_out, and_7_out, and_8_out, and_9_out, and_10_out,
       and_11_out, and_12_out, and_13_out, and_14_out, and_15_out, and_16_out, n4_bit_adder_1_cout,
       n4_bit_adder_1_s1, n4_bit_adder_1_s2, n4_bit_adder_1_s3, n4_bit_adder_2_cout, n4_bit_adder_2_s1,
       n4_bit_adder_2_s2, n4_bit_adder_2_s3;

  and and_1 (S1, B1, A1);
  and and_2 (and_2_out, B2, A1);
  and and_3 (and_3_out, B3, A1);
  and and_4 (and_4_out, B4, A1);
  and and_5 (and_5_out, B1, A2);
  and and_6 (and_6_out, B2, A2);
  and and_7 (and_7_out, B3, A2);
  and and_8 (and_8_out, B4, A2);
  and and_9 (and_9_out, B1, A3);
  and and_10 (and_10_out, B2, A3);
  and and_11 (and_11_out, B3, A3);
  and and_12 (and_12_out, B4, A3);
  and and_13 (and_13_out, B1, A4);
  and and_14 (and_14_out, B2, A4);
  and and_15 (and_15_out, B3, A4);
  and and_16 (and_16_out, B4, A4);
  _4_bit_Adder u_4_bit_adder_1 (
    .Cout(n4_bit_adder_1_cout), .A3(Cin), .A2(and_4_out), .A1(and_3_out), .A0(and_2_out), .B3(and_8_out),
    .B2(and_7_out), .B1(and_6_out), .B0(and_5_out), .Cin(Cin), .S3(n4_bit_adder_1_s3),
    .S2(n4_bit_adder_1_s2), .S1(n4_bit_adder_1_s1), .S0(S2));
  _4_bit_Adder u_4_bit_adder_2 (
    .Cout(n4_bit_adder_2_cout), .A3(n4_bit_adder_1_cout), .A2(n4_bit_adder_1_s3), .A1(n4_bit_adder_1_s2),
    .A0(n4_bit_adder_1_s1), .B3(and_12_out), .B2(and_11_out), .B1(and_10_out), .B0(and_9_out), .Cin(Cin),
    .S3(n4_bit_adder_2_s3), .S2(n4_bit_adder_2_s2), .S1(n4_bit_adder_2_s1), .S0(S3));
  _4_bit_Adder u_4_bit_adder_3 (
    .Cout(S8), .A3(n4_bit_adder_2_cout), .A2(n4_bit_adder_2_s3), .A1(n4_bit_adder_2_s2),
    .A0(n4_bit_adder_2_s1), .B3(and_16_out), .B2(and_15_out), .B1(and_14_out), .B0(and_13_out), .Cin(Cin),
    .S3(S7), .S2(S6), .S1(S5), .S0(S4));
  // Probe on {S8, S7, S6, S5, S4, S3, S2, S1}
endmodule

module _8_bit_Adder (
  input  Cin,
  input  A7,
  input  A6,
  input  A5,
  input  A4,
  input  A3,
  input  A2,
  input  A1,
  input  A0,
  input  B7,
  input  B6,
  input  B5,
  input  B4,
  input  B3,
  input  B2,
  input  B1,
  input  B0,
  output S7,
  output S6,
  output S5,
  output S4,
  output S3,
  output S2,
  output S1,
  output S0,
  output Cout
);

  wire n4_bit_adder_1_cout;

  _4_bit_Adder u_4_bit_adder_1 (
    .Cout(n4_bit_adder_1_cout), .A3(A3), .A2(A2), .A1(A1), .A0(A0), .B3(B3), .B2(B2), .B1(B1), .B0(B0),
    .Cin(Cin), .S3(S3), .S2(S2), .S1(S1), .S0(S0));
  _4_bit_Adder u_4_bit_adder_2 (
    .Cout(Cout), .A3(A7), .A2(A6), .A1(A5), .A0(A4), .B3(B7), .B2(B6), .B1(B5), .B0(B4),
    .Cin(n4_bit_adder_1_cout), .S3(S7), .S2(S6), .S1(S5), .S0(S4));
endmodule

module _8x8_Multiplier (
  input  A1,
  input  A8,
  input  A7,
  input  A6,
  input  A5,
  input  A4,
  input  A3,
  input  A2,
  input  A1_2,
  input  B8,
  input  B7,
  input  B6,
  input  B5,
  input  B4,
  input  B3,
  input  B2,
  input  B1,
  output P16,
  output P15,
  output P14,
  output P13,
  output P12,
  output P11,
  output P10,
  output P9,
  output P8,
  output P7,
  output P6,
  output P5,
  output P4,
  output P3,
  output P2,
  output P1
);

  wire and_2_out, and_3_out, and_4_out, and_5_out, and_6_out, and_7_out, and_8_out, and_9_out, and_10_out,
       and_11_out, and_12_out, and_13_out, and_14_out, and_15_out, and_16_out, and_17_out, and_18_out,
       and_19_out, and_20_out, and_21_out, and_22_out, and_23_out, and_24_out, and_25_out, and_26_out,
       and_27_out, and_28_out, and_29_out, and_30_out, and_31_out, and_32_out, and_33_out, and_34_out,
       and_35_out, and_36_out, and_37_out, and_38_out, and_39_out, and_40_out, and_41_out, and_42_out,
       and_43_out, and_44_out, and_45_out, and_46_out, and_47_out, and_48_out, and_49_out, and_50_out,
       and_51_out, and_52_out, and_53_out, and_54_out, and_55_out, and_56_out, and_57_out, and_58_out,
       and_59_out, and_60_out, and_61_out, and_62_out, and_63_out, and_64_out, n8_bit_adder_1_cout,
       n8_bit_adder_1_s1, n8_bit_adder_1_s2, n8_bit_adder_1_s3, n8_bit_adder_1_s4, n8_bit_adder_1_s5,
       n8_bit_adder_1_s6, n8_bit_adder_1_s7, n8_bit_adder_2_cout, n8_bit_adder_2_s1, n8_bit_adder_2_s2,
       n8_bit_adder_2_s3, n8_bit_adder_2_s4, n8_bit_adder_2_s5, n8_bit_adder_2_s6, n8_bit_adder_2_s7,
       n8_bit_adder_3_cout, n8_bit_adder_3_s1, n8_bit_adder_3_s2, n8_bit_adder_3_s3, n8_bit_adder_3_s4,
       n8_bit_adder_3_s5, n8_bit_adder_3_s6, n8_bit_adder_3_s7, n8_bit_adder_4_cout, n8_bit_adder_4_s1,
       n8_bit_adder_4_s2, n8_bit_adder_4_s3, n8_bit_adder_4_s4, n8_bit_adder_4_s5, n8_bit_adder_4_s6,
       n8_bit_adder_4_s7, n8_bit_adder_5_cout, n8_bit_adder_5_s1, n8_bit_adder_5_s2, n8_bit_adder_5_s3,
       n8_bit_adder_5_s4, n8_bit_adder_5_s5, n8_bit_adder_5_s6, n8_bit_adder_5_s7, n8_bit_adder_6_cout,
       n8_bit_adder_6_s1, n8_bit_adder_6_s2, n8_bit_adder_6_s3, n8_bit_adder_6_s4, n8_bit_adder_6_s5,
       n8_bit_adder_6_s6, n8_bit_adder_6_s7;

  // Probe on {A8, A7, A6, A5, A4, A3, A2, A1_2}
  // Probe on {B8, B7, B6, B5, B4, B3, B2, B1}
  and and_1 (P1, B1, A1_2);
  and and_2 (and_2_out, B2, A1_2);
  and and_3 (and_3_out, B3, A1_2);
  and and_4 (and_4_out, B4, A1_2);
  and and_5 (and_5_out, B5, A1_2);
  and and_6 (and_6_out, B6, A1_2);
  and and_7 (and_7_out, B7, A1_2);
  and and_8 (and_8_out, B8, A1_2);
  and and_9 (and_9_out, B1, A2);
  and and_10 (and_10_out, B2, A2);
  and and_11 (and_11_out, B3, A2);
  and and_12 (and_12_out, B4, A2);
  and and_13 (and_13_out, B5, A2);
  and and_14 (and_14_out, B6, A2);
  and and_15 (and_15_out, B7, A2);
  and and_16 (and_16_out, B8, A2);
  and and_17 (and_17_out, B1, A3);
  and and_18 (and_18_out, B2, A3);
  and and_19 (and_19_out, B3, A3);
  and and_20 (and_20_out, B4, A3);
  and and_21 (and_21_out, B5, A3);
  and and_22 (and_22_out, B6, A3);
  and and_23 (and_23_out, B7, A3);
  and and_24 (and_24_out, B8, A3);
  and and_25 (and_25_out, B1, A4);
  and and_26 (and_26_out, B2, A4);
  and and_27 (and_27_out, B3, A4);
  and and_28 (and_28_out, B4, A4);
  and and_29 (and_29_out, B5, A4);
  and and_30 (and_30_out, B6, A4);
  and and_31 (and_31_out, B7, A4);
  and and_32 (and_32_out, B8, A4);
  and and_33 (and_33_out, B1, A5);
  and and_34 (and_34_out, B2, A5);
  and and_35 (and_35_out, B3, A5);
  and and_36 (and_36_out, B4, A5);
  and and_37 (and_37_out, B5, A5);
  and and_38 (and_38_out, B6, A5);
  and and_39 (and_39_out, B7, A5);
  and and_40 (and_40_out, B8, A5);
  and and_41 (and_41_out, B1, A6);
  and and_42 (and_42_out, B2, A6);
  and and_43 (and_43_out, B3, A6);
  and and_44 (and_44_out, B4, A6);
  and and_45 (and_45_out, B5, A6);
  and and_46 (and_46_out, B6, A6);
  and and_47 (and_47_out, B7, A6);
  and and_48 (and_48_out, B8, A6);
  and and_49 (and_49_out, B1, A7);
  and and_50 (and_50_out, B2, A7);
  and and_51 (and_51_out, B3, A7);
  and and_52 (and_52_out, B4, A7);
  and and_53 (and_53_out, B5, A7);
  and and_54 (and_54_out, B6, A7);
  and and_55 (and_55_out, B7, A7);
  and and_56 (and_56_out, B8, A7);
  and and_57 (and_57_out, B1, A8);
  and and_58 (and_58_out, B2, A8);
  and and_59 (and_59_out, B3, A8);
  and and_60 (and_60_out, B4, A8);
  and and_61 (and_61_out, B5, A8);
  and and_62 (and_62_out, B6, A8);
  and and_63 (and_63_out, B7, A8);
  and and_64 (and_64_out, B8, A8);
  _8_bit_Adder u_8_bit_adder_1 (
    .Cout(n8_bit_adder_1_cout), .A7(A1), .A6(and_8_out), .A5(and_7_out), .A4(and_6_out), .A3(and_5_out),
    .A2(and_4_out), .A1(and_3_out), .A0(and_2_out), .B7(and_16_out), .B6(and_15_out), .B5(and_14_out),
    .B4(and_13_out), .B3(and_12_out), .B2(and_11_out), .B1(and_10_out), .B0(and_9_out), .Cin(A1),
    .S7(n8_bit_adder_1_s7), .S6(n8_bit_adder_1_s6), .S5(n8_bit_adder_1_s5), .S4(n8_bit_adder_1_s4),
    .S3(n8_bit_adder_1_s3), .S2(n8_bit_adder_1_s2), .S1(n8_bit_adder_1_s1), .S0(P2));
  _8_bit_Adder u_8_bit_adder_2 (
    .Cout(n8_bit_adder_2_cout), .A7(n8_bit_adder_1_cout), .A6(n8_bit_adder_1_s7), .A5(n8_bit_adder_1_s6),
    .A4(n8_bit_adder_1_s5), .A3(n8_bit_adder_1_s4), .A2(n8_bit_adder_1_s3), .A1(n8_bit_adder_1_s2),
    .A0(n8_bit_adder_1_s1), .B7(and_24_out), .B6(and_23_out), .B5(and_22_out), .B4(and_21_out),
    .B3(and_20_out), .B2(and_19_out), .B1(and_18_out), .B0(and_17_out), .Cin(A1), .S7(n8_bit_adder_2_s7),
    .S6(n8_bit_adder_2_s6), .S5(n8_bit_adder_2_s5), .S4(n8_bit_adder_2_s4), .S3(n8_bit_adder_2_s3),
    .S2(n8_bit_adder_2_s2), .S1(n8_bit_adder_2_s1), .S0(P3));
  _8_bit_Adder u_8_bit_adder_3 (
    .Cout(n8_bit_adder_3_cout), .A7(n8_bit_adder_2_cout), .A6(n8_bit_adder_2_s7), .A5(n8_bit_adder_2_s6),
    .A4(n8_bit_adder_2_s5), .A3(n8_bit_adder_2_s4), .A2(n8_bit_adder_2_s3), .A1(n8_bit_adder_2_s2),
    .A0(n8_bit_adder_2_s1), .B7(and_32_out), .B6(and_31_out), .B5(and_30_out), .B4(and_29_out),
    .B3(and_28_out), .B2(and_27_out), .B1(and_26_out), .B0(and_25_out), .Cin(A1), .S7(n8_bit_adder_3_s7),
    .S6(n8_bit_adder_3_s6), .S5(n8_bit_adder_3_s5), .S4(n8_bit_adder_3_s4), .S3(n8_bit_adder_3_s3),
    .S2(n8_bit_adder_3_s2), .S1(n8_bit_adder_3_s1), .S0(P4));
  _8_bit_Adder u_8_bit_adder_4 (
    .Cout(n8_bit_adder_4_cout), .A7(n8_bit_adder_3_cout), .A6(n8_bit_adder_3_s7), .A5(n8_bit_adder_3_s6),
    .A4(n8_bit_adder_3_s5), .A3(n8_bit_adder_3_s4), .A2(n8_bit_adder_3_s3), .A1(n8_bit_adder_3_s2),
    .A0(n8_bit_adder_3_s1), .B7(and_40_out), .B6(and_39_out), .B5(and_38_out), .B4(and_37_out),
    .B3(and_36_out), .B2(and_35_out), .B1(and_34_out), .B0(and_33_out), .Cin(A1), .S7(n8_bit_adder_4_s7),
    .S6(n8_bit_adder_4_s6), .S5(n8_bit_adder_4_s5), .S4(n8_bit_adder_4_s4), .S3(n8_bit_adder_4_s3),
    .S2(n8_bit_adder_4_s2), .S1(n8_bit_adder_4_s1), .S0(P5));
  _8_bit_Adder u_8_bit_adder_5 (
    .Cout(n8_bit_adder_5_cout), .A7(n8_bit_adder_4_cout), .A6(n8_bit_adder_4_s7), .A5(n8_bit_adder_4_s6),
    .A4(n8_bit_adder_4_s5), .A3(n8_bit_adder_4_s4), .A2(n8_bit_adder_4_s3), .A1(n8_bit_adder_4_s2),
    .A0(n8_bit_adder_4_s1), .B7(and_48_out), .B6(and_47_out), .B5(and_46_out), .B4(and_45_out),
    .B3(and_44_out), .B2(and_43_out), .B1(and_42_out), .B0(and_41_out), .Cin(A1), .S7(n8_bit_adder_5_s7),
    .S6(n8_bit_adder_5_s6), .S5(n8_bit_adder_5_s5), .S4(n8_bit_adder_5_s4), .S3(n8_bit_adder_5_s3),
    .S2(n8_bit_adder_5_s2), .S1(n8_bit_adder_5_s1), .S0(P6));
  _8_bit_Adder u_8_bit_adder_6 (
    .Cout(n8_bit_adder_6_cout), .A7(n8_bit_adder_5_cout), .A6(n8_bit_adder_5_s7), .A5(n8_bit_adder_5_s6),
    .A4(n8_bit_adder_5_s5), .A3(n8_bit_adder_5_s4), .A2(n8_bit_adder_5_s3), .A1(n8_bit_adder_5_s2),
    .A0(n8_bit_adder_5_s1), .B7(and_56_out), .B6(and_55_out), .B5(and_54_out), .B4(and_53_out),
    .B3(and_52_out), .B2(and_51_out), .B1(and_50_out), .B0(and_49_out), .Cin(A1), .S7(n8_bit_adder_6_s7),
    .S6(n8_bit_adder_6_s6), .S5(n8_bit_adder_6_s5), .S4(n8_bit_adder_6_s4), .S3(n8_bit_adder_6_s3),
    .S2(n8_bit_adder_6_s2), .S1(n8_bit_adder_6_s1), .S0(P7));
  _8_bit_Adder u_8_bit_adder_7 (
    .Cout(P16), .A7(n8_bit_adder_6_cout), .A6(n8_bit_adder_6_s7), .A5(n8_bit_adder_6_s6),
    .A4(n8_bit_adder_6_s5), .A3(n8_bit_adder_6_s4), .A2(n8_bit_adder_6_s3), .A1(n8_bit_adder_6_s2),
    .A0(n8_bit_adder_6_s1), .B7(and_64_out), .B6(and_63_out), .B5(and_62_out), .B4(and_61_out),
    .B3(and_60_out), .B2(and_59_out), .B1(and_58_out), .B0(and_57_out), .Cin(A1), .S7(P15), .S6(P14),
    .S5(P13), .S4(P12), .S3(P11), .S2(P10), .S1(P9), .S0(P8));
  // Probe on {P16, P15, P14, P13, P12, P11, P10, P9, P8, P7, P6, P5, P4, P3, P2, P1}
endmodule

module _1_bit_ALU (
  input  Sub_Cin,
  input  Add_Cin,
  input  A,
  input  A_inv,
  input  B,
  input  B_inv,
  input  [2:0] Selector,
  output Result,
  output Adder_Cout,
  output Sub_Cout
);

  wire and_1_out, comparator_1_lt, multiplexer_1_out, multiplexer_2_out, multiplier_1_out, n1_bit_adder_1_s,
       n1_bit_adder_2_s, not_1_out, not_2_out, or_1_out;

  not not_1 (not_1_out, A);
  not not_2 (not_2_out, B);
  Multiplexer #(.enable("false")) multiplexer_1 (.in0(A), .in1(not_1_out), .out(multiplexer_1_out), .sel(A_inv));
  Multiplexer #(.enable("false")) multiplexer_2 (.in0(B), .in1(not_2_out), .out(multiplexer_2_out), .sel(B_inv));
  and and_1 (and_1_out, multiplexer_1_out, multiplexer_2_out);
  or or_1 (or_1_out, multiplexer_1_out, multiplexer_2_out);
  _1_bit_Adder u_1_bit_adder_1 (
    .B(multiplexer_2_out), .Cin(Add_Cin), .S(n1_bit_adder_1_s), .Cout(Adder_Cout), .A(multiplexer_1_out));
  Multiplier #(.width(1)) multiplier_1 (
    .a(multiplexer_1_out), .b(multiplexer_2_out), .out(multiplier_1_out));  // open: cin, cout
  _1_bit_Adder u_1_bit_adder_2 (
    .B(multiplexer_2_out), .Cin(Sub_Cin), .S(n1_bit_adder_2_s), .Cout(Sub_Cout), .A(multiplexer_1_out));
  Comparator #(.width(1)) comparator_1 (
    .a(multiplexer_1_out), .b(multiplexer_2_out), .lt(comparator_1_lt));  // open: gt, eq
  Multiplexer #(.select(3), .enable("false")) multiplexer_3 (
    .in0(and_1_out), .in1(or_1_out), .in2(n1_bit_adder_1_s), .in3(multiplier_1_out), .in6(n1_bit_adder_2_s),
    .in7(comparator_1_lt), .out(Result), .sel(Selector));  // open: in4, in5
endmodule

module _4_bit_ALU (
  input  A3,
  input  A2,
  input  A1,
  input  A0,
  input  B3,
  input  B2,
  input  B1,
  input  B0,
  input  A_inv,
  input  B_inv,
  input  Sub_Cin,
  input  Add_Cin,
  input  [1:0] ALUOp,
  input  [3:0] F3F2F1F0,
  output F3,
  output F2,
  output F1,
  output F0,
  output Sub_Cout,
  output Add_Cout
);

  wire n1_bit_alu_1_adder_cout, n1_bit_alu_1_sub_cout, n1_bit_alu_2_adder_cout, n1_bit_alu_2_sub_cout,
       n1_bit_alu_3_adder_cout, n1_bit_alu_3_sub_cout;
  wire [2:0] alu_controle_unit_1_alu_controle_output;

  ALU_Controle_Unit alu_controle_unit_1 (
    .ALU_Controle_Output(alu_controle_unit_1_alu_controle_output), .F3(F3F2F1F0[3]), .F2(F3F2F1F0[2]),
    .F1(F3F2F1F0[1]), .F0(F3F2F1F0[0]), .Op1(ALUOp[1]), .Op0(ALUOp[0]));
  _1_bit_ALU u_1_bit_alu_1 (
    .A(A0), .A_inv(A_inv), .B(B0), .B_inv(B_inv), .Result(F0), .Adder_Cout(n1_bit_alu_1_adder_cout),
    .Sub_Cout(n1_bit_alu_1_sub_cout), .Sub_Cin(Sub_Cin), .Add_Cin(Add_Cin),
    .Selector(alu_controle_unit_1_alu_controle_output));
  _1_bit_ALU u_1_bit_alu_2 (
    .A(A1), .A_inv(A_inv), .B(B1), .B_inv(B_inv), .Result(F1), .Adder_Cout(n1_bit_alu_2_adder_cout),
    .Sub_Cout(n1_bit_alu_2_sub_cout), .Sub_Cin(n1_bit_alu_1_sub_cout), .Add_Cin(n1_bit_alu_1_adder_cout),
    .Selector(alu_controle_unit_1_alu_controle_output));
  _1_bit_ALU u_1_bit_alu_3 (
    .A(A2), .A_inv(A_inv), .B(B2), .B_inv(B_inv), .Result(F2), .Adder_Cout(n1_bit_alu_3_adder_cout),
    .Sub_Cout(n1_bit_alu_3_sub_cout), .Sub_Cin(n1_bit_alu_2_sub_cout), .Add_Cin(n1_bit_alu_2_adder_cout),
    .Selector(alu_controle_unit_1_alu_controle_output));
  _1_bit_ALU u_1_bit_alu_4 (
    .A(A3), .A_inv(A_inv), .B(B3), .B_inv(B_inv), .Result(F3), .Adder_Cout(Add_Cout), .Sub_Cout(Sub_Cout),
    .Sub_Cin(n1_bit_alu_3_sub_cout), .Add_Cin(n1_bit_alu_3_adder_cout),
    .Selector(alu_controle_unit_1_alu_controle_output));
endmodule

module ALU_Controle_Unit (
  input  F3,
  input  F2,
  input  F1,
  input  F0,
  input  Op1,
  input  Op0,
  output [2:0] ALU_Controle_Output
);

  wire and_1_out, or_1_out;

  or or_1 (or_1_out, F3, F0);
  and and_1 (and_1_out, Op1, F1);
  and and_2 (ALU_Controle_Output[0], Op1, or_1_out);
  or or_2 (ALU_Controle_Output[2], Op0, and_1_out);
  or or_3 (ALU_Controle_Output[1], ~Op1, ~F2);  // OR_Gate
endmodule

module _32_bit_LU (
  input  [1:0] S1S0,
  input  [31:0] A,
  input  [31:0] B,
  output [31:0] Output
);

  _4_bit_LU u_4_bit_lu_1 (.S1S0(S1S0), .A(A[3:0]), .B(B[3:0]), .Result(Output[3:0]));
  _4_bit_LU u_4_bit_lu_2 (.S1S0(S1S0), .A(A[7:4]), .B(B[7:4]), .Result(Output[7:4]));
  _4_bit_LU u_4_bit_lu_3 (.S1S0(S1S0), .A(A[11:8]), .B(B[11:8]), .Result(Output[11:8]));
  _4_bit_LU u_4_bit_lu_4 (.S1S0(S1S0), .A(A[15:12]), .B(B[15:12]), .Result(Output[15:12]));
  _4_bit_LU u_4_bit_lu_5 (.S1S0(S1S0), .A(A[19:16]), .B(B[19:16]), .Result(Output[19:16]));
  _4_bit_LU u_4_bit_lu_6 (.S1S0(S1S0), .A(A[23:20]), .B(B[23:20]), .Result(Output[23:20]));
  _4_bit_LU u_4_bit_lu_7 (.S1S0(S1S0), .A(A[27:24]), .B(B[27:24]), .Result(Output[27:24]));
  _4_bit_LU u_4_bit_lu_8 (.S1S0(S1S0), .A(A[31:28]), .B(B[31:28]), .Result(Output[31:28]));

  // Notes on the sheet:
  //   Operations
  //   AND
  //   OR
  //   XOR
  //   NOT
  //   00
  //   01
  //   10
  //   11
  //   S1S0
endmodule

module _32_bit_Arithmetic_Unit (
  input  [1:0] S1S0,
  input  Cin,
  input  [31:0] A,
  input  [31:0] B,
  output Cout,
  output [31:0] Output
);

  wire n16_bit_arithmetic_unit_1_cout;

  // Probe on A
  // Probe on B
  _16_bit_Arithmetic_Unit u_16_bit_arithmetic_unit_1 (
    .A15(A[15]), .A14(A[14]), .A13(A[13]), .A12(A[12]), .A11(A[11]), .A10(A[10]), .A9(A[9]), .A8(A[8]),
    .A7(A[7]), .A6(A[6]), .A5(A[5]), .A4(A[4]), .A3(A[3]), .A2(A[2]), .A1(A[1]), .A0(A[0]), .B15(B[15]),
    .B14(B[14]), .B13(B[13]), .B12(B[12]), .B11(B[11]), .B10(B[10]), .B9(B[9]), .B8(B[8]), .B7(B[7]),
    .B6(B[6]), .B5(B[5]), .B4(B[4]), .B3(B[3]), .B2(B[2]), .B1(B[1]), .B0(B[0]), .S1S0(S1S0), .Cin(Cin),
    .Cout(n16_bit_arithmetic_unit_1_cout), .S15(Output[15]), .S14(Output[14]), .S13(Output[13]),
    .S12(Output[12]), .S11(Output[11]), .S10(Output[10]), .S9(Output[9]), .S8(Output[8]), .S7(Output[7]),
    .S6(Output[6]), .S5(Output[5]), .S4(Output[4]), .S3(Output[3]), .S2(Output[2]), .S1(Output[1]),
    .S0(Output[0]));
  _16_bit_Arithmetic_Unit u_16_bit_arithmetic_unit_2 (
    .A15(A[31]), .A14(A[30]), .A13(A[29]), .A12(A[28]), .A11(A[27]), .A10(A[26]), .A9(A[25]), .A8(A[24]),
    .A7(A[23]), .A6(A[22]), .A5(A[21]), .A4(A[20]), .A3(A[19]), .A2(A[18]), .A1(A[17]), .A0(A[16]),
    .B15(B[31]), .B14(B[30]), .B13(B[29]), .B12(B[28]), .B11(B[27]), .B10(B[26]), .B9(B[25]), .B8(B[24]),
    .B7(B[23]), .B6(B[22]), .B5(B[21]), .B4(B[20]), .B3(B[19]), .B2(B[18]), .B1(B[17]), .B0(B[16]),
    .S1S0(S1S0), .Cin(n16_bit_arithmetic_unit_1_cout), .Cout(Cout), .S15(Output[31]), .S14(Output[30]),
    .S13(Output[29]), .S12(Output[28]), .S11(Output[27]), .S10(Output[26]), .S9(Output[25]), .S8(Output[24]),
    .S7(Output[23]), .S6(Output[22]), .S5(Output[21]), .S4(Output[20]), .S3(Output[19]), .S2(Output[18]),
    .S1(Output[17]), .S0(Output[16]));
  // Probe on Output
endmodule

module _16_bit_Adder (
  input  A15,
  input  A14,
  input  A13,
  input  A12,
  input  A11,
  input  A10,
  input  A9,
  input  A8,
  input  A7,
  input  A6,
  input  A5,
  input  A4,
  input  A3,
  input  A2,
  input  A1,
  input  A0,
  input  B15,
  input  B14,
  input  B13,
  input  B12,
  input  B11,
  input  B10,
  input  B9,
  input  B8,
  input  B7,
  input  B6,
  input  B5,
  input  B4,
  input  B3,
  input  B2,
  input  B1,
  input  B0,
  input  Cin,
  output S15,
  output S14,
  output S13,
  output S12,
  output S11,
  output S10,
  output S9,
  output S8,
  output S7,
  output S6,
  output S5,
  output S4,
  output S3,
  output S2,
  output S1,
  output S0,
  output Cout
);

  wire n8_bit_adder_1_cout;

  _8_bit_Adder u_8_bit_adder_1 (
    .Cout(n8_bit_adder_1_cout), .A7(A7), .A6(A6), .A5(A5), .A4(A4), .A3(A3), .A2(A2), .A1(A1), .A0(A0),
    .B7(B7), .B6(B6), .B5(B5), .B4(B4), .B3(B3), .B2(B2), .B1(B1), .B0(B0), .Cin(Cin), .S7(S7), .S6(S6),
    .S5(S5), .S4(S4), .S3(S3), .S2(S2), .S1(S1), .S0(S0));
  _8_bit_Adder u_8_bit_adder_2 (
    .Cout(Cout), .A7(A15), .A6(A14), .A5(A13), .A4(A12), .A3(A11), .A2(A10), .A1(A9), .A0(A8), .B7(B15),
    .B6(B14), .B5(B13), .B4(B12), .B3(B11), .B2(B10), .B1(B9), .B0(B8), .Cin(n8_bit_adder_1_cout), .S7(S15),
    .S6(S14), .S5(S13), .S4(S12), .S3(S11), .S2(S10), .S1(S9), .S0(S8));
endmodule

module _16x16_Multiplier (
  input  [15:0] A,
  input  [15:0] B,
  output [31:0] Output
);

  wire and_2_out, and_3_out, and_4_out, and_5_out, and_6_out, and_7_out, and_8_out, and_9_out, and_10_out,
       and_11_out, and_12_out, and_13_out, and_14_out, and_15_out, and_16_out, and_17_out, and_18_out,
       and_19_out, and_20_out, and_21_out, and_22_out, and_23_out, and_24_out, and_25_out, and_26_out,
       and_27_out, and_28_out, and_29_out, and_30_out, and_31_out, and_32_out, and_33_out, and_34_out,
       and_35_out, and_36_out, and_37_out, and_38_out, and_39_out, and_40_out, and_41_out, and_42_out,
       and_43_out, and_44_out, and_45_out, and_46_out, and_47_out, and_48_out, and_49_out, and_50_out,
       and_51_out, and_52_out, and_53_out, and_54_out, and_55_out, and_56_out, and_57_out, and_58_out,
       and_59_out, and_60_out, and_61_out, and_62_out, and_63_out, and_64_out, and_65_out, and_66_out,
       and_67_out, and_68_out, and_69_out, and_70_out, and_71_out, and_72_out, and_73_out, and_74_out,
       and_75_out, and_76_out, and_77_out, and_78_out, and_79_out, and_80_out, and_81_out, and_82_out,
       and_83_out, and_84_out, and_85_out, and_86_out, and_87_out, and_88_out, and_89_out, and_90_out,
       and_91_out, and_92_out, and_93_out, and_94_out, and_95_out, and_96_out, and_97_out, and_98_out,
       and_99_out, and_100_out, and_101_out, and_102_out, and_103_out, and_104_out, and_105_out, and_106_out,
       and_107_out, and_108_out, and_109_out, and_110_out, and_111_out, and_112_out, and_113_out,
       and_114_out, and_115_out, and_116_out, and_117_out, and_118_out, and_119_out, and_120_out,
       and_121_out, and_122_out, and_123_out, and_124_out, and_125_out, and_126_out, and_127_out,
       and_128_out, and_129_out, and_130_out, and_131_out, and_132_out, and_133_out, and_134_out,
       and_135_out, and_136_out, and_137_out, and_138_out, and_139_out, and_140_out, and_141_out,
       and_142_out, and_143_out, and_144_out, and_145_out, and_146_out, and_147_out, and_148_out,
       and_149_out, and_150_out, and_151_out, and_152_out, and_153_out, and_154_out, and_155_out,
       and_156_out, and_157_out, and_158_out, and_159_out, and_160_out, and_161_out, and_162_out,
       and_163_out, and_164_out, and_165_out, and_166_out, and_167_out, and_168_out, and_169_out,
       and_170_out, and_171_out, and_172_out, and_173_out, and_174_out, and_175_out, and_176_out,
       and_177_out, and_178_out, and_179_out, and_180_out, and_181_out, and_182_out, and_183_out,
       and_184_out, and_185_out, and_186_out, and_187_out, and_188_out, and_189_out, and_190_out,
       and_191_out, and_192_out, and_193_out, and_194_out, and_195_out, and_196_out, and_197_out,
       and_198_out, and_199_out, and_200_out, and_201_out, and_202_out, and_203_out, and_204_out,
       and_205_out, and_206_out, and_207_out, and_208_out, and_209_out, and_210_out, and_211_out,
       and_212_out, and_213_out, and_214_out, and_215_out, and_216_out, and_217_out, and_218_out,
       and_219_out, and_220_out, and_221_out, and_222_out, and_223_out, and_224_out, and_225_out,
       and_226_out, and_227_out, and_228_out, and_229_out, and_230_out, and_231_out, and_232_out,
       and_233_out, and_234_out, and_235_out, and_236_out, and_237_out, and_238_out, and_239_out,
       and_240_out, and_241_out, and_242_out, and_243_out, and_244_out, and_245_out, and_246_out,
       and_247_out, and_248_out, and_249_out, and_250_out, and_251_out, and_252_out, and_253_out,
       and_254_out, and_255_out, and_256_out, n16_bit_adder_1_cout, n16_bit_adder_1_s1, n16_bit_adder_1_s2,
       n16_bit_adder_1_s3, n16_bit_adder_1_s4, n16_bit_adder_1_s5, n16_bit_adder_1_s6, n16_bit_adder_1_s7,
       n16_bit_adder_1_s8, n16_bit_adder_1_s9, n16_bit_adder_1_s10, n16_bit_adder_1_s11, n16_bit_adder_1_s12,
       n16_bit_adder_1_s13, n16_bit_adder_1_s14, n16_bit_adder_1_s15, n16_bit_adder_2_cout,
       n16_bit_adder_2_s1, n16_bit_adder_2_s2, n16_bit_adder_2_s3, n16_bit_adder_2_s4, n16_bit_adder_2_s5,
       n16_bit_adder_2_s6, n16_bit_adder_2_s7, n16_bit_adder_2_s8, n16_bit_adder_2_s9, n16_bit_adder_2_s10,
       n16_bit_adder_2_s11, n16_bit_adder_2_s12, n16_bit_adder_2_s13, n16_bit_adder_2_s14,
       n16_bit_adder_2_s15, n16_bit_adder_3_cout, n16_bit_adder_3_s1, n16_bit_adder_3_s2, n16_bit_adder_3_s3,
       n16_bit_adder_3_s4, n16_bit_adder_3_s5, n16_bit_adder_3_s6, n16_bit_adder_3_s7, n16_bit_adder_3_s8,
       n16_bit_adder_3_s9, n16_bit_adder_3_s10, n16_bit_adder_3_s11, n16_bit_adder_3_s12,
       n16_bit_adder_3_s13, n16_bit_adder_3_s14, n16_bit_adder_3_s15, n16_bit_adder_4_cout,
       n16_bit_adder_4_s1, n16_bit_adder_4_s2, n16_bit_adder_4_s3, n16_bit_adder_4_s4, n16_bit_adder_4_s5,
       n16_bit_adder_4_s6, n16_bit_adder_4_s7, n16_bit_adder_4_s8, n16_bit_adder_4_s9, n16_bit_adder_4_s10,
       n16_bit_adder_4_s11, n16_bit_adder_4_s12, n16_bit_adder_4_s13, n16_bit_adder_4_s14,
       n16_bit_adder_4_s15, n16_bit_adder_5_cout, n16_bit_adder_5_s1, n16_bit_adder_5_s2, n16_bit_adder_5_s3,
       n16_bit_adder_5_s4, n16_bit_adder_5_s5, n16_bit_adder_5_s6, n16_bit_adder_5_s7, n16_bit_adder_5_s8,
       n16_bit_adder_5_s9, n16_bit_adder_5_s10, n16_bit_adder_5_s11, n16_bit_adder_5_s12,
       n16_bit_adder_5_s13, n16_bit_adder_5_s14, n16_bit_adder_5_s15, n16_bit_adder_6_cout,
       n16_bit_adder_6_s1, n16_bit_adder_6_s2, n16_bit_adder_6_s3, n16_bit_adder_6_s4, n16_bit_adder_6_s5,
       n16_bit_adder_6_s6, n16_bit_adder_6_s7, n16_bit_adder_6_s8, n16_bit_adder_6_s9, n16_bit_adder_6_s10,
       n16_bit_adder_6_s11, n16_bit_adder_6_s12, n16_bit_adder_6_s13, n16_bit_adder_6_s14,
       n16_bit_adder_6_s15, n16_bit_adder_7_cout, n16_bit_adder_7_s1, n16_bit_adder_7_s2, n16_bit_adder_7_s3,
       n16_bit_adder_7_s4, n16_bit_adder_7_s5, n16_bit_adder_7_s6, n16_bit_adder_7_s7, n16_bit_adder_7_s8,
       n16_bit_adder_7_s9, n16_bit_adder_7_s10, n16_bit_adder_7_s11, n16_bit_adder_7_s12,
       n16_bit_adder_7_s13, n16_bit_adder_7_s14, n16_bit_adder_7_s15, n16_bit_adder_8_cout,
       n16_bit_adder_8_s1, n16_bit_adder_8_s2, n16_bit_adder_8_s3, n16_bit_adder_8_s4, n16_bit_adder_8_s5,
       n16_bit_adder_8_s6, n16_bit_adder_8_s7, n16_bit_adder_8_s8, n16_bit_adder_8_s9, n16_bit_adder_8_s10,
       n16_bit_adder_8_s11, n16_bit_adder_8_s12, n16_bit_adder_8_s13, n16_bit_adder_8_s14,
       n16_bit_adder_8_s15, n16_bit_adder_9_cout, n16_bit_adder_9_s1, n16_bit_adder_9_s2, n16_bit_adder_9_s3,
       n16_bit_adder_9_s4, n16_bit_adder_9_s5, n16_bit_adder_9_s6, n16_bit_adder_9_s7, n16_bit_adder_9_s8,
       n16_bit_adder_9_s9, n16_bit_adder_9_s10, n16_bit_adder_9_s11, n16_bit_adder_9_s12,
       n16_bit_adder_9_s13, n16_bit_adder_9_s14, n16_bit_adder_9_s15, n16_bit_adder_10_cout,
       n16_bit_adder_10_s1, n16_bit_adder_10_s2, n16_bit_adder_10_s3, n16_bit_adder_10_s4,
       n16_bit_adder_10_s5, n16_bit_adder_10_s6, n16_bit_adder_10_s7, n16_bit_adder_10_s8,
       n16_bit_adder_10_s9, n16_bit_adder_10_s10, n16_bit_adder_10_s11, n16_bit_adder_10_s12,
       n16_bit_adder_10_s13, n16_bit_adder_10_s14, n16_bit_adder_10_s15, n16_bit_adder_11_cout,
       n16_bit_adder_11_s1, n16_bit_adder_11_s2, n16_bit_adder_11_s3, n16_bit_adder_11_s4,
       n16_bit_adder_11_s5, n16_bit_adder_11_s6, n16_bit_adder_11_s7, n16_bit_adder_11_s8,
       n16_bit_adder_11_s9, n16_bit_adder_11_s10, n16_bit_adder_11_s11, n16_bit_adder_11_s12,
       n16_bit_adder_11_s13, n16_bit_adder_11_s14, n16_bit_adder_11_s15, n16_bit_adder_12_cout,
       n16_bit_adder_12_s1, n16_bit_adder_12_s2, n16_bit_adder_12_s3, n16_bit_adder_12_s4,
       n16_bit_adder_12_s5, n16_bit_adder_12_s6, n16_bit_adder_12_s7, n16_bit_adder_12_s8,
       n16_bit_adder_12_s9, n16_bit_adder_12_s10, n16_bit_adder_12_s11, n16_bit_adder_12_s12,
       n16_bit_adder_12_s13, n16_bit_adder_12_s14, n16_bit_adder_12_s15, n16_bit_adder_13_cout,
       n16_bit_adder_13_s1, n16_bit_adder_13_s2, n16_bit_adder_13_s3, n16_bit_adder_13_s4,
       n16_bit_adder_13_s5, n16_bit_adder_13_s6, n16_bit_adder_13_s7, n16_bit_adder_13_s8,
       n16_bit_adder_13_s9, n16_bit_adder_13_s10, n16_bit_adder_13_s11, n16_bit_adder_13_s12,
       n16_bit_adder_13_s13, n16_bit_adder_13_s14, n16_bit_adder_13_s15, n16_bit_adder_14_cout,
       n16_bit_adder_14_s1, n16_bit_adder_14_s2, n16_bit_adder_14_s3, n16_bit_adder_14_s4,
       n16_bit_adder_14_s5, n16_bit_adder_14_s6, n16_bit_adder_14_s7, n16_bit_adder_14_s8,
       n16_bit_adder_14_s9, n16_bit_adder_14_s10, n16_bit_adder_14_s11, n16_bit_adder_14_s12,
       n16_bit_adder_14_s13, n16_bit_adder_14_s14, n16_bit_adder_14_s15;

  // Probe on A
  // Probe on B
  // Probe on Output
  and and_1 (Output[0], B[0], A[0]);
  and and_2 (and_2_out, B[1], A[0]);
  and and_3 (and_3_out, B[2], A[0]);
  and and_4 (and_4_out, B[3], A[0]);
  and and_5 (and_5_out, B[4], A[0]);
  and and_6 (and_6_out, B[5], A[0]);
  and and_7 (and_7_out, B[6], A[0]);
  and and_8 (and_8_out, B[7], A[0]);
  and and_9 (and_9_out, B[8], A[0]);
  and and_10 (and_10_out, B[9], A[0]);
  and and_11 (and_11_out, B[10], A[0]);
  and and_12 (and_12_out, B[11], A[0]);
  and and_13 (and_13_out, B[12], A[0]);
  and and_14 (and_14_out, B[13], A[0]);
  and and_15 (and_15_out, B[14], A[0]);
  and and_16 (and_16_out, B[15], A[0]);
  and and_17 (and_17_out, B[0], A[1]);
  and and_18 (and_18_out, B[1], A[1]);
  and and_19 (and_19_out, B[2], A[1]);
  and and_20 (and_20_out, B[3], A[1]);
  and and_21 (and_21_out, B[4], A[1]);
  and and_22 (and_22_out, B[5], A[1]);
  and and_23 (and_23_out, B[6], A[1]);
  and and_24 (and_24_out, B[7], A[1]);
  and and_25 (and_25_out, B[8], A[1]);
  and and_26 (and_26_out, B[9], A[1]);
  and and_27 (and_27_out, B[10], A[1]);
  and and_28 (and_28_out, B[11], A[1]);
  and and_29 (and_29_out, B[12], A[1]);
  and and_30 (and_30_out, B[13], A[1]);
  and and_31 (and_31_out, B[14], A[1]);
  and and_32 (and_32_out, B[15], A[1]);
  and and_33 (and_33_out, B[0], A[2]);
  and and_34 (and_34_out, B[1], A[2]);
  and and_35 (and_35_out, B[2], A[2]);
  and and_36 (and_36_out, B[3], A[2]);
  and and_37 (and_37_out, B[4], A[2]);
  and and_38 (and_38_out, B[5], A[2]);
  and and_39 (and_39_out, B[6], A[2]);
  and and_40 (and_40_out, B[7], A[2]);
  and and_41 (and_41_out, B[8], A[2]);
  and and_42 (and_42_out, B[9], A[2]);
  and and_43 (and_43_out, B[10], A[2]);
  and and_44 (and_44_out, B[11], A[2]);
  and and_45 (and_45_out, B[12], A[2]);
  and and_46 (and_46_out, B[13], A[2]);
  and and_47 (and_47_out, B[14], A[2]);
  and and_48 (and_48_out, B[15], A[2]);
  and and_49 (and_49_out, B[0], A[3]);
  and and_50 (and_50_out, B[1], A[3]);
  and and_51 (and_51_out, B[2], A[3]);
  and and_52 (and_52_out, B[3], A[3]);
  and and_53 (and_53_out, B[4], A[3]);
  and and_54 (and_54_out, B[5], A[3]);
  and and_55 (and_55_out, B[6], A[3]);
  and and_56 (and_56_out, B[7], A[3]);
  and and_57 (and_57_out, B[8], A[3]);
  and and_58 (and_58_out, B[9], A[3]);
  and and_59 (and_59_out, B[10], A[3]);
  and and_60 (and_60_out, B[11], A[3]);
  and and_61 (and_61_out, B[12], A[3]);
  and and_62 (and_62_out, B[13], A[3]);
  and and_63 (and_63_out, B[14], A[3]);
  and and_64 (and_64_out, B[15], A[3]);
  and and_65 (and_65_out, B[0], A[4]);
  and and_66 (and_66_out, B[1], A[4]);
  and and_67 (and_67_out, B[2], A[4]);
  and and_68 (and_68_out, B[3], A[4]);
  and and_69 (and_69_out, B[4], A[4]);
  and and_70 (and_70_out, B[5], A[4]);
  and and_71 (and_71_out, B[6], A[4]);
  and and_72 (and_72_out, B[7], A[4]);
  and and_73 (and_73_out, B[8], A[4]);
  and and_74 (and_74_out, B[9], A[4]);
  and and_75 (and_75_out, B[10], A[4]);
  and and_76 (and_76_out, B[11], A[4]);
  and and_77 (and_77_out, B[12], A[4]);
  and and_78 (and_78_out, B[13], A[4]);
  and and_79 (and_79_out, B[14], A[4]);
  and and_80 (and_80_out, B[15], A[4]);
  and and_81 (and_81_out, B[0], A[5]);
  and and_82 (and_82_out, B[1], A[5]);
  and and_83 (and_83_out, B[2], A[5]);
  and and_84 (and_84_out, B[3], A[5]);
  and and_85 (and_85_out, B[4], A[5]);
  and and_86 (and_86_out, B[5], A[5]);
  and and_87 (and_87_out, B[6], A[5]);
  and and_88 (and_88_out, B[7], A[5]);
  and and_89 (and_89_out, B[8], A[5]);
  and and_90 (and_90_out, B[9], A[5]);
  and and_91 (and_91_out, B[10], A[5]);
  and and_92 (and_92_out, B[11], A[5]);
  and and_93 (and_93_out, B[12], A[5]);
  and and_94 (and_94_out, B[13], A[5]);
  and and_95 (and_95_out, B[14], A[5]);
  and and_96 (and_96_out, B[15], A[5]);
  and and_97 (and_97_out, B[0], A[6]);
  and and_98 (and_98_out, B[1], A[6]);
  and and_99 (and_99_out, B[2], A[6]);
  and and_100 (and_100_out, B[3], A[6]);
  and and_101 (and_101_out, B[4], A[6]);
  and and_102 (and_102_out, B[5], A[6]);
  and and_103 (and_103_out, B[6], A[6]);
  and and_104 (and_104_out, B[7], A[6]);
  and and_105 (and_105_out, B[8], A[6]);
  and and_106 (and_106_out, B[9], A[6]);
  and and_107 (and_107_out, B[10], A[6]);
  and and_108 (and_108_out, B[11], A[6]);
  and and_109 (and_109_out, B[12], A[6]);
  and and_110 (and_110_out, B[13], A[6]);
  and and_111 (and_111_out, B[14], A[6]);
  and and_112 (and_112_out, B[15], A[6]);
  and and_113 (and_113_out, B[0], A[7]);
  and and_114 (and_114_out, B[1], A[7]);
  and and_115 (and_115_out, B[2], A[7]);
  and and_116 (and_116_out, B[3], A[7]);
  and and_117 (and_117_out, B[4], A[7]);
  and and_118 (and_118_out, B[5], A[7]);
  and and_119 (and_119_out, B[6], A[7]);
  and and_120 (and_120_out, B[7], A[7]);
  and and_121 (and_121_out, B[8], A[7]);
  and and_122 (and_122_out, B[9], A[7]);
  and and_123 (and_123_out, B[10], A[7]);
  and and_124 (and_124_out, B[11], A[7]);
  and and_125 (and_125_out, B[12], A[7]);
  and and_126 (and_126_out, B[13], A[7]);
  and and_127 (and_127_out, B[14], A[7]);
  and and_128 (and_128_out, B[15], A[7]);
  and and_129 (and_129_out, B[0], A[8]);
  and and_130 (and_130_out, B[1], A[8]);
  and and_131 (and_131_out, B[2], A[8]);
  and and_132 (and_132_out, B[3], A[8]);
  and and_133 (and_133_out, B[4], A[8]);
  and and_134 (and_134_out, B[5], A[8]);
  and and_135 (and_135_out, B[6], A[8]);
  and and_136 (and_136_out, B[7], A[8]);
  and and_137 (and_137_out, B[8], A[8]);
  and and_138 (and_138_out, B[9], A[8]);
  and and_139 (and_139_out, B[10], A[8]);
  and and_140 (and_140_out, B[11], A[8]);
  and and_141 (and_141_out, B[12], A[8]);
  and and_142 (and_142_out, B[13], A[8]);
  and and_143 (and_143_out, B[14], A[8]);
  and and_144 (and_144_out, B[15], A[8]);
  and and_145 (and_145_out, B[0], A[9]);
  and and_146 (and_146_out, B[1], A[9]);
  and and_147 (and_147_out, B[2], A[9]);
  and and_148 (and_148_out, B[3], A[9]);
  and and_149 (and_149_out, B[4], A[9]);
  and and_150 (and_150_out, B[5], A[9]);
  and and_151 (and_151_out, B[6], A[9]);
  and and_152 (and_152_out, B[7], A[9]);
  and and_153 (and_153_out, B[8], A[9]);
  and and_154 (and_154_out, B[9], A[9]);
  and and_155 (and_155_out, B[10], A[9]);
  and and_156 (and_156_out, B[11], A[9]);
  and and_157 (and_157_out, B[12], A[9]);
  and and_158 (and_158_out, B[13], A[9]);
  and and_159 (and_159_out, B[14], A[9]);
  and and_160 (and_160_out, B[15], A[9]);
  and and_161 (and_161_out, B[0], A[10]);
  and and_162 (and_162_out, B[1], A[10]);
  and and_163 (and_163_out, B[2], A[10]);
  and and_164 (and_164_out, B[3], A[10]);
  and and_165 (and_165_out, B[4], A[10]);
  and and_166 (and_166_out, B[5], A[10]);
  and and_167 (and_167_out, B[6], A[10]);
  and and_168 (and_168_out, B[7], A[10]);
  and and_169 (and_169_out, B[8], A[10]);
  and and_170 (and_170_out, B[9], A[10]);
  and and_171 (and_171_out, B[10], A[10]);
  and and_172 (and_172_out, B[11], A[10]);
  and and_173 (and_173_out, B[12], A[10]);
  and and_174 (and_174_out, B[13], A[10]);
  and and_175 (and_175_out, B[14], A[10]);
  and and_176 (and_176_out, B[15], A[10]);
  and and_177 (and_177_out, B[0], A[11]);
  and and_178 (and_178_out, B[1], A[11]);
  and and_179 (and_179_out, B[2], A[11]);
  and and_180 (and_180_out, B[3], A[11]);
  and and_181 (and_181_out, B[4], A[11]);
  and and_182 (and_182_out, B[5], A[11]);
  and and_183 (and_183_out, B[6], A[11]);
  and and_184 (and_184_out, B[7], A[11]);
  and and_185 (and_185_out, B[8], A[11]);
  and and_186 (and_186_out, B[9], A[11]);
  and and_187 (and_187_out, B[10], A[11]);
  and and_188 (and_188_out, B[11], A[11]);
  and and_189 (and_189_out, B[12], A[11]);
  and and_190 (and_190_out, B[13], A[11]);
  and and_191 (and_191_out, B[14], A[11]);
  and and_192 (and_192_out, B[15], A[11]);
  and and_193 (and_193_out, B[0], A[12]);
  and and_194 (and_194_out, B[1], A[12]);
  and and_195 (and_195_out, B[2], A[12]);
  and and_196 (and_196_out, B[3], A[12]);
  and and_197 (and_197_out, B[4], A[12]);
  and and_198 (and_198_out, B[5], A[12]);
  and and_199 (and_199_out, B[6], A[12]);
  and and_200 (and_200_out, B[7], A[12]);
  and and_201 (and_201_out, B[8], A[12]);
  and and_202 (and_202_out, B[9], A[12]);
  and and_203 (and_203_out, B[10], A[12]);
  and and_204 (and_204_out, B[11], A[12]);
  and and_205 (and_205_out, B[12], A[12]);
  and and_206 (and_206_out, B[13], A[12]);
  and and_207 (and_207_out, B[14], A[12]);
  and and_208 (and_208_out, B[15], A[12]);
  and and_209 (and_209_out, B[0], A[13]);
  and and_210 (and_210_out, B[1], A[13]);
  and and_211 (and_211_out, B[2], A[13]);
  and and_212 (and_212_out, B[3], A[13]);
  and and_213 (and_213_out, B[4], A[13]);
  and and_214 (and_214_out, B[5], A[13]);
  and and_215 (and_215_out, B[6], A[13]);
  and and_216 (and_216_out, B[7], A[13]);
  and and_217 (and_217_out, B[8], A[13]);
  and and_218 (and_218_out, B[9], A[13]);
  and and_219 (and_219_out, B[10], A[13]);
  and and_220 (and_220_out, B[11], A[13]);
  and and_221 (and_221_out, B[12], A[13]);
  and and_222 (and_222_out, B[13], A[13]);
  and and_223 (and_223_out, B[14], A[13]);
  and and_224 (and_224_out, B[15], A[13]);
  and and_225 (and_225_out, B[0], A[14]);
  and and_226 (and_226_out, B[1], A[14]);
  and and_227 (and_227_out, B[2], A[14]);
  and and_228 (and_228_out, B[3], A[14]);
  and and_229 (and_229_out, B[4], A[14]);
  and and_230 (and_230_out, B[5], A[14]);
  and and_231 (and_231_out, B[6], A[14]);
  and and_232 (and_232_out, B[7], A[14]);
  and and_233 (and_233_out, B[8], A[14]);
  and and_234 (and_234_out, B[9], A[14]);
  and and_235 (and_235_out, B[10], A[14]);
  and and_236 (and_236_out, B[11], A[14]);
  and and_237 (and_237_out, B[12], A[14]);
  and and_238 (and_238_out, B[13], A[14]);
  and and_239 (and_239_out, B[14], A[14]);
  and and_240 (and_240_out, B[15], A[14]);
  and and_241 (and_241_out, B[0], A[15]);
  and and_242 (and_242_out, B[1], A[15]);
  and and_243 (and_243_out, B[2], A[15]);
  and and_244 (and_244_out, B[3], A[15]);
  and and_245 (and_245_out, B[4], A[15]);
  and and_246 (and_246_out, B[5], A[15]);
  and and_247 (and_247_out, B[6], A[15]);
  and and_248 (and_248_out, B[7], A[15]);
  and and_249 (and_249_out, B[8], A[15]);
  and and_250 (and_250_out, B[9], A[15]);
  and and_251 (and_251_out, B[10], A[15]);
  and and_252 (and_252_out, B[11], A[15]);
  and and_253 (and_253_out, B[12], A[15]);
  and and_254 (and_254_out, B[13], A[15]);
  and and_255 (and_255_out, B[14], A[15]);
  and and_256 (and_256_out, B[15], A[15]);
  _16_bit_Adder u_16_bit_adder_1 (
    .A15(1'b0), .A14(and_16_out), .A13(and_15_out), .A12(and_14_out), .A11(and_13_out), .A10(and_12_out),
    .A9(and_11_out), .A8(and_10_out), .A7(and_9_out), .A6(and_8_out), .A5(and_7_out), .A4(and_6_out),
    .A3(and_5_out), .A2(and_4_out), .A1(and_3_out), .A0(and_2_out), .B15(and_32_out), .B14(and_31_out),
    .B13(and_30_out), .B12(and_29_out), .B11(and_28_out), .B10(and_27_out), .B9(and_26_out), .B8(and_25_out),
    .B7(and_24_out), .B6(and_23_out), .B5(and_22_out), .B4(and_21_out), .B3(and_20_out), .B2(and_19_out),
    .B1(and_18_out), .B0(and_17_out), .Cin(1'b0), .Cout(n16_bit_adder_1_cout), .S15(n16_bit_adder_1_s15),
    .S14(n16_bit_adder_1_s14), .S13(n16_bit_adder_1_s13), .S12(n16_bit_adder_1_s12),
    .S11(n16_bit_adder_1_s11), .S10(n16_bit_adder_1_s10), .S9(n16_bit_adder_1_s9), .S8(n16_bit_adder_1_s8),
    .S7(n16_bit_adder_1_s7), .S6(n16_bit_adder_1_s6), .S5(n16_bit_adder_1_s5), .S4(n16_bit_adder_1_s4),
    .S3(n16_bit_adder_1_s3), .S2(n16_bit_adder_1_s2), .S1(n16_bit_adder_1_s1), .S0(Output[1]));
  _16_bit_Adder u_16_bit_adder_2 (
    .A15(n16_bit_adder_1_cout), .A14(n16_bit_adder_1_s15), .A13(n16_bit_adder_1_s14),
    .A12(n16_bit_adder_1_s13), .A11(n16_bit_adder_1_s12), .A10(n16_bit_adder_1_s11),
    .A9(n16_bit_adder_1_s10), .A8(n16_bit_adder_1_s9), .A7(n16_bit_adder_1_s8), .A6(n16_bit_adder_1_s7),
    .A5(n16_bit_adder_1_s6), .A4(n16_bit_adder_1_s5), .A3(n16_bit_adder_1_s4), .A2(n16_bit_adder_1_s3),
    .A1(n16_bit_adder_1_s2), .A0(n16_bit_adder_1_s1), .B15(and_48_out), .B14(and_47_out), .B13(and_46_out),
    .B12(and_45_out), .B11(and_44_out), .B10(and_43_out), .B9(and_42_out), .B8(and_41_out), .B7(and_40_out),
    .B6(and_39_out), .B5(and_38_out), .B4(and_37_out), .B3(and_36_out), .B2(and_35_out), .B1(and_34_out),
    .B0(and_33_out), .Cin(1'b0), .Cout(n16_bit_adder_2_cout), .S15(n16_bit_adder_2_s15),
    .S14(n16_bit_adder_2_s14), .S13(n16_bit_adder_2_s13), .S12(n16_bit_adder_2_s12),
    .S11(n16_bit_adder_2_s11), .S10(n16_bit_adder_2_s10), .S9(n16_bit_adder_2_s9), .S8(n16_bit_adder_2_s8),
    .S7(n16_bit_adder_2_s7), .S6(n16_bit_adder_2_s6), .S5(n16_bit_adder_2_s5), .S4(n16_bit_adder_2_s4),
    .S3(n16_bit_adder_2_s3), .S2(n16_bit_adder_2_s2), .S1(n16_bit_adder_2_s1), .S0(Output[2]));
  _16_bit_Adder u_16_bit_adder_3 (
    .A15(n16_bit_adder_2_cout), .A14(n16_bit_adder_2_s15), .A13(n16_bit_adder_2_s14),
    .A12(n16_bit_adder_2_s13), .A11(n16_bit_adder_2_s12), .A10(n16_bit_adder_2_s11),
    .A9(n16_bit_adder_2_s10), .A8(n16_bit_adder_2_s9), .A7(n16_bit_adder_2_s8), .A6(n16_bit_adder_2_s7),
    .A5(n16_bit_adder_2_s6), .A4(n16_bit_adder_2_s5), .A3(n16_bit_adder_2_s4), .A2(n16_bit_adder_2_s3),
    .A1(n16_bit_adder_2_s2), .A0(n16_bit_adder_2_s1), .B15(and_64_out), .B14(and_63_out), .B13(and_62_out),
    .B12(and_61_out), .B11(and_60_out), .B10(and_59_out), .B9(and_58_out), .B8(and_57_out), .B7(and_56_out),
    .B6(and_55_out), .B5(and_54_out), .B4(and_53_out), .B3(and_52_out), .B2(and_51_out), .B1(and_50_out),
    .B0(and_49_out), .Cin(1'b0), .Cout(n16_bit_adder_3_cout), .S15(n16_bit_adder_3_s15),
    .S14(n16_bit_adder_3_s14), .S13(n16_bit_adder_3_s13), .S12(n16_bit_adder_3_s12),
    .S11(n16_bit_adder_3_s11), .S10(n16_bit_adder_3_s10), .S9(n16_bit_adder_3_s9), .S8(n16_bit_adder_3_s8),
    .S7(n16_bit_adder_3_s7), .S6(n16_bit_adder_3_s6), .S5(n16_bit_adder_3_s5), .S4(n16_bit_adder_3_s4),
    .S3(n16_bit_adder_3_s3), .S2(n16_bit_adder_3_s2), .S1(n16_bit_adder_3_s1), .S0(Output[3]));
  _16_bit_Adder u_16_bit_adder_4 (
    .A15(n16_bit_adder_3_cout), .A14(n16_bit_adder_3_s15), .A13(n16_bit_adder_3_s14),
    .A12(n16_bit_adder_3_s13), .A11(n16_bit_adder_3_s12), .A10(n16_bit_adder_3_s11),
    .A9(n16_bit_adder_3_s10), .A8(n16_bit_adder_3_s9), .A7(n16_bit_adder_3_s8), .A6(n16_bit_adder_3_s7),
    .A5(n16_bit_adder_3_s6), .A4(n16_bit_adder_3_s5), .A3(n16_bit_adder_3_s4), .A2(n16_bit_adder_3_s3),
    .A1(n16_bit_adder_3_s2), .A0(n16_bit_adder_3_s1), .B15(and_80_out), .B14(and_79_out), .B13(and_78_out),
    .B12(and_77_out), .B11(and_76_out), .B10(and_75_out), .B9(and_74_out), .B8(and_73_out), .B7(and_72_out),
    .B6(and_71_out), .B5(and_70_out), .B4(and_69_out), .B3(and_68_out), .B2(and_67_out), .B1(and_66_out),
    .B0(and_65_out), .Cin(1'b0), .Cout(n16_bit_adder_4_cout), .S15(n16_bit_adder_4_s15),
    .S14(n16_bit_adder_4_s14), .S13(n16_bit_adder_4_s13), .S12(n16_bit_adder_4_s12),
    .S11(n16_bit_adder_4_s11), .S10(n16_bit_adder_4_s10), .S9(n16_bit_adder_4_s9), .S8(n16_bit_adder_4_s8),
    .S7(n16_bit_adder_4_s7), .S6(n16_bit_adder_4_s6), .S5(n16_bit_adder_4_s5), .S4(n16_bit_adder_4_s4),
    .S3(n16_bit_adder_4_s3), .S2(n16_bit_adder_4_s2), .S1(n16_bit_adder_4_s1), .S0(Output[4]));
  _16_bit_Adder u_16_bit_adder_5 (
    .A15(n16_bit_adder_4_cout), .A14(n16_bit_adder_4_s15), .A13(n16_bit_adder_4_s14),
    .A12(n16_bit_adder_4_s13), .A11(n16_bit_adder_4_s12), .A10(n16_bit_adder_4_s11),
    .A9(n16_bit_adder_4_s10), .A8(n16_bit_adder_4_s9), .A7(n16_bit_adder_4_s8), .A6(n16_bit_adder_4_s7),
    .A5(n16_bit_adder_4_s6), .A4(n16_bit_adder_4_s5), .A3(n16_bit_adder_4_s4), .A2(n16_bit_adder_4_s3),
    .A1(n16_bit_adder_4_s2), .A0(n16_bit_adder_4_s1), .B15(and_96_out), .B14(and_95_out), .B13(and_94_out),
    .B12(and_93_out), .B11(and_92_out), .B10(and_91_out), .B9(and_90_out), .B8(and_89_out), .B7(and_88_out),
    .B6(and_87_out), .B5(and_86_out), .B4(and_85_out), .B3(and_84_out), .B2(and_83_out), .B1(and_82_out),
    .B0(and_81_out), .Cin(1'b0), .Cout(n16_bit_adder_5_cout), .S15(n16_bit_adder_5_s15),
    .S14(n16_bit_adder_5_s14), .S13(n16_bit_adder_5_s13), .S12(n16_bit_adder_5_s12),
    .S11(n16_bit_adder_5_s11), .S10(n16_bit_adder_5_s10), .S9(n16_bit_adder_5_s9), .S8(n16_bit_adder_5_s8),
    .S7(n16_bit_adder_5_s7), .S6(n16_bit_adder_5_s6), .S5(n16_bit_adder_5_s5), .S4(n16_bit_adder_5_s4),
    .S3(n16_bit_adder_5_s3), .S2(n16_bit_adder_5_s2), .S1(n16_bit_adder_5_s1), .S0(Output[5]));
  _16_bit_Adder u_16_bit_adder_6 (
    .A15(n16_bit_adder_5_cout), .A14(n16_bit_adder_5_s15), .A13(n16_bit_adder_5_s14),
    .A12(n16_bit_adder_5_s13), .A11(n16_bit_adder_5_s12), .A10(n16_bit_adder_5_s11),
    .A9(n16_bit_adder_5_s10), .A8(n16_bit_adder_5_s9), .A7(n16_bit_adder_5_s8), .A6(n16_bit_adder_5_s7),
    .A5(n16_bit_adder_5_s6), .A4(n16_bit_adder_5_s5), .A3(n16_bit_adder_5_s4), .A2(n16_bit_adder_5_s3),
    .A1(n16_bit_adder_5_s2), .A0(n16_bit_adder_5_s1), .B15(and_112_out), .B14(and_111_out),
    .B13(and_110_out), .B12(and_109_out), .B11(and_108_out), .B10(and_107_out), .B9(and_106_out),
    .B8(and_105_out), .B7(and_104_out), .B6(and_103_out), .B5(and_102_out), .B4(and_101_out),
    .B3(and_100_out), .B2(and_99_out), .B1(and_98_out), .B0(and_97_out), .Cin(1'b0),
    .Cout(n16_bit_adder_6_cout), .S15(n16_bit_adder_6_s15), .S14(n16_bit_adder_6_s14),
    .S13(n16_bit_adder_6_s13), .S12(n16_bit_adder_6_s12), .S11(n16_bit_adder_6_s11),
    .S10(n16_bit_adder_6_s10), .S9(n16_bit_adder_6_s9), .S8(n16_bit_adder_6_s8), .S7(n16_bit_adder_6_s7),
    .S6(n16_bit_adder_6_s6), .S5(n16_bit_adder_6_s5), .S4(n16_bit_adder_6_s4), .S3(n16_bit_adder_6_s3),
    .S2(n16_bit_adder_6_s2), .S1(n16_bit_adder_6_s1), .S0(Output[6]));
  _16_bit_Adder u_16_bit_adder_7 (
    .A15(n16_bit_adder_6_cout), .A14(n16_bit_adder_6_s15), .A13(n16_bit_adder_6_s14),
    .A12(n16_bit_adder_6_s13), .A11(n16_bit_adder_6_s12), .A10(n16_bit_adder_6_s11),
    .A9(n16_bit_adder_6_s10), .A8(n16_bit_adder_6_s9), .A7(n16_bit_adder_6_s8), .A6(n16_bit_adder_6_s7),
    .A5(n16_bit_adder_6_s6), .A4(n16_bit_adder_6_s5), .A3(n16_bit_adder_6_s4), .A2(n16_bit_adder_6_s3),
    .A1(n16_bit_adder_6_s2), .A0(n16_bit_adder_6_s1), .B15(and_128_out), .B14(and_127_out),
    .B13(and_126_out), .B12(and_125_out), .B11(and_124_out), .B10(and_123_out), .B9(and_122_out),
    .B8(and_121_out), .B7(and_120_out), .B6(and_119_out), .B5(and_118_out), .B4(and_117_out),
    .B3(and_116_out), .B2(and_115_out), .B1(and_114_out), .B0(and_113_out), .Cin(1'b0),
    .Cout(n16_bit_adder_7_cout), .S15(n16_bit_adder_7_s15), .S14(n16_bit_adder_7_s14),
    .S13(n16_bit_adder_7_s13), .S12(n16_bit_adder_7_s12), .S11(n16_bit_adder_7_s11),
    .S10(n16_bit_adder_7_s10), .S9(n16_bit_adder_7_s9), .S8(n16_bit_adder_7_s8), .S7(n16_bit_adder_7_s7),
    .S6(n16_bit_adder_7_s6), .S5(n16_bit_adder_7_s5), .S4(n16_bit_adder_7_s4), .S3(n16_bit_adder_7_s3),
    .S2(n16_bit_adder_7_s2), .S1(n16_bit_adder_7_s1), .S0(Output[7]));
  _16_bit_Adder u_16_bit_adder_8 (
    .A15(n16_bit_adder_7_cout), .A14(n16_bit_adder_7_s15), .A13(n16_bit_adder_7_s14),
    .A12(n16_bit_adder_7_s13), .A11(n16_bit_adder_7_s12), .A10(n16_bit_adder_7_s11),
    .A9(n16_bit_adder_7_s10), .A8(n16_bit_adder_7_s9), .A7(n16_bit_adder_7_s8), .A6(n16_bit_adder_7_s7),
    .A5(n16_bit_adder_7_s6), .A4(n16_bit_adder_7_s5), .A3(n16_bit_adder_7_s4), .A2(n16_bit_adder_7_s3),
    .A1(n16_bit_adder_7_s2), .A0(n16_bit_adder_7_s1), .B15(and_144_out), .B14(and_143_out),
    .B13(and_142_out), .B12(and_141_out), .B11(and_140_out), .B10(and_139_out), .B9(and_138_out),
    .B8(and_137_out), .B7(and_136_out), .B6(and_135_out), .B5(and_134_out), .B4(and_133_out),
    .B3(and_132_out), .B2(and_131_out), .B1(and_130_out), .B0(and_129_out), .Cin(1'b0),
    .Cout(n16_bit_adder_8_cout), .S15(n16_bit_adder_8_s15), .S14(n16_bit_adder_8_s14),
    .S13(n16_bit_adder_8_s13), .S12(n16_bit_adder_8_s12), .S11(n16_bit_adder_8_s11),
    .S10(n16_bit_adder_8_s10), .S9(n16_bit_adder_8_s9), .S8(n16_bit_adder_8_s8), .S7(n16_bit_adder_8_s7),
    .S6(n16_bit_adder_8_s6), .S5(n16_bit_adder_8_s5), .S4(n16_bit_adder_8_s4), .S3(n16_bit_adder_8_s3),
    .S2(n16_bit_adder_8_s2), .S1(n16_bit_adder_8_s1), .S0(Output[8]));
  _16_bit_Adder u_16_bit_adder_9 (
    .A15(n16_bit_adder_8_cout), .A14(n16_bit_adder_8_s15), .A13(n16_bit_adder_8_s14),
    .A12(n16_bit_adder_8_s13), .A11(n16_bit_adder_8_s12), .A10(n16_bit_adder_8_s11),
    .A9(n16_bit_adder_8_s10), .A8(n16_bit_adder_8_s9), .A7(n16_bit_adder_8_s8), .A6(n16_bit_adder_8_s7),
    .A5(n16_bit_adder_8_s6), .A4(n16_bit_adder_8_s5), .A3(n16_bit_adder_8_s4), .A2(n16_bit_adder_8_s3),
    .A1(n16_bit_adder_8_s2), .A0(n16_bit_adder_8_s1), .B15(and_160_out), .B14(and_159_out),
    .B13(and_158_out), .B12(and_157_out), .B11(and_156_out), .B10(and_155_out), .B9(and_154_out),
    .B8(and_153_out), .B7(and_152_out), .B6(and_151_out), .B5(and_150_out), .B4(and_149_out),
    .B3(and_148_out), .B2(and_147_out), .B1(and_146_out), .B0(and_145_out), .Cin(1'b0),
    .Cout(n16_bit_adder_9_cout), .S15(n16_bit_adder_9_s15), .S14(n16_bit_adder_9_s14),
    .S13(n16_bit_adder_9_s13), .S12(n16_bit_adder_9_s12), .S11(n16_bit_adder_9_s11),
    .S10(n16_bit_adder_9_s10), .S9(n16_bit_adder_9_s9), .S8(n16_bit_adder_9_s8), .S7(n16_bit_adder_9_s7),
    .S6(n16_bit_adder_9_s6), .S5(n16_bit_adder_9_s5), .S4(n16_bit_adder_9_s4), .S3(n16_bit_adder_9_s3),
    .S2(n16_bit_adder_9_s2), .S1(n16_bit_adder_9_s1), .S0(Output[9]));
  _16_bit_Adder u_16_bit_adder_10 (
    .A15(n16_bit_adder_9_cout), .A14(n16_bit_adder_9_s15), .A13(n16_bit_adder_9_s14),
    .A12(n16_bit_adder_9_s13), .A11(n16_bit_adder_9_s12), .A10(n16_bit_adder_9_s11),
    .A9(n16_bit_adder_9_s10), .A8(n16_bit_adder_9_s9), .A7(n16_bit_adder_9_s8), .A6(n16_bit_adder_9_s7),
    .A5(n16_bit_adder_9_s6), .A4(n16_bit_adder_9_s5), .A3(n16_bit_adder_9_s4), .A2(n16_bit_adder_9_s3),
    .A1(n16_bit_adder_9_s2), .A0(n16_bit_adder_9_s1), .B15(and_176_out), .B14(and_175_out),
    .B13(and_174_out), .B12(and_173_out), .B11(and_172_out), .B10(and_171_out), .B9(and_170_out),
    .B8(and_169_out), .B7(and_168_out), .B6(and_167_out), .B5(and_166_out), .B4(and_165_out),
    .B3(and_164_out), .B2(and_163_out), .B1(and_162_out), .B0(and_161_out), .Cin(1'b0),
    .Cout(n16_bit_adder_10_cout), .S15(n16_bit_adder_10_s15), .S14(n16_bit_adder_10_s14),
    .S13(n16_bit_adder_10_s13), .S12(n16_bit_adder_10_s12), .S11(n16_bit_adder_10_s11),
    .S10(n16_bit_adder_10_s10), .S9(n16_bit_adder_10_s9), .S8(n16_bit_adder_10_s8), .S7(n16_bit_adder_10_s7),
    .S6(n16_bit_adder_10_s6), .S5(n16_bit_adder_10_s5), .S4(n16_bit_adder_10_s4), .S3(n16_bit_adder_10_s3),
    .S2(n16_bit_adder_10_s2), .S1(n16_bit_adder_10_s1), .S0(Output[10]));
  _16_bit_Adder u_16_bit_adder_11 (
    .A15(n16_bit_adder_10_cout), .A14(n16_bit_adder_10_s15), .A13(n16_bit_adder_10_s14),
    .A12(n16_bit_adder_10_s13), .A11(n16_bit_adder_10_s12), .A10(n16_bit_adder_10_s11),
    .A9(n16_bit_adder_10_s10), .A8(n16_bit_adder_10_s9), .A7(n16_bit_adder_10_s8), .A6(n16_bit_adder_10_s7),
    .A5(n16_bit_adder_10_s6), .A4(n16_bit_adder_10_s5), .A3(n16_bit_adder_10_s4), .A2(n16_bit_adder_10_s3),
    .A1(n16_bit_adder_10_s2), .A0(n16_bit_adder_10_s1), .B15(and_192_out), .B14(and_191_out),
    .B13(and_190_out), .B12(and_189_out), .B11(and_188_out), .B10(and_187_out), .B9(and_186_out),
    .B8(and_185_out), .B7(and_184_out), .B6(and_183_out), .B5(and_182_out), .B4(and_181_out),
    .B3(and_180_out), .B2(and_179_out), .B1(and_178_out), .B0(and_177_out), .Cin(1'b0),
    .Cout(n16_bit_adder_11_cout), .S15(n16_bit_adder_11_s15), .S14(n16_bit_adder_11_s14),
    .S13(n16_bit_adder_11_s13), .S12(n16_bit_adder_11_s12), .S11(n16_bit_adder_11_s11),
    .S10(n16_bit_adder_11_s10), .S9(n16_bit_adder_11_s9), .S8(n16_bit_adder_11_s8), .S7(n16_bit_adder_11_s7),
    .S6(n16_bit_adder_11_s6), .S5(n16_bit_adder_11_s5), .S4(n16_bit_adder_11_s4), .S3(n16_bit_adder_11_s3),
    .S2(n16_bit_adder_11_s2), .S1(n16_bit_adder_11_s1), .S0(Output[11]));
  _16_bit_Adder u_16_bit_adder_12 (
    .A15(n16_bit_adder_11_cout), .A14(n16_bit_adder_11_s15), .A13(n16_bit_adder_11_s14),
    .A12(n16_bit_adder_11_s13), .A11(n16_bit_adder_11_s12), .A10(n16_bit_adder_11_s11),
    .A9(n16_bit_adder_11_s10), .A8(n16_bit_adder_11_s9), .A7(n16_bit_adder_11_s8), .A6(n16_bit_adder_11_s7),
    .A5(n16_bit_adder_11_s6), .A4(n16_bit_adder_11_s5), .A3(n16_bit_adder_11_s4), .A2(n16_bit_adder_11_s3),
    .A1(n16_bit_adder_11_s2), .A0(n16_bit_adder_11_s1), .B15(and_208_out), .B14(and_207_out),
    .B13(and_206_out), .B12(and_205_out), .B11(and_204_out), .B10(and_203_out), .B9(and_202_out),
    .B8(and_201_out), .B7(and_200_out), .B6(and_199_out), .B5(and_198_out), .B4(and_197_out),
    .B3(and_196_out), .B2(and_195_out), .B1(and_194_out), .B0(and_193_out), .Cin(1'b0),
    .Cout(n16_bit_adder_12_cout), .S15(n16_bit_adder_12_s15), .S14(n16_bit_adder_12_s14),
    .S13(n16_bit_adder_12_s13), .S12(n16_bit_adder_12_s12), .S11(n16_bit_adder_12_s11),
    .S10(n16_bit_adder_12_s10), .S9(n16_bit_adder_12_s9), .S8(n16_bit_adder_12_s8), .S7(n16_bit_adder_12_s7),
    .S6(n16_bit_adder_12_s6), .S5(n16_bit_adder_12_s5), .S4(n16_bit_adder_12_s4), .S3(n16_bit_adder_12_s3),
    .S2(n16_bit_adder_12_s2), .S1(n16_bit_adder_12_s1), .S0(Output[12]));
  _16_bit_Adder u_16_bit_adder_13 (
    .A15(n16_bit_adder_12_cout), .A14(n16_bit_adder_12_s15), .A13(n16_bit_adder_12_s14),
    .A12(n16_bit_adder_12_s13), .A11(n16_bit_adder_12_s12), .A10(n16_bit_adder_12_s11),
    .A9(n16_bit_adder_12_s10), .A8(n16_bit_adder_12_s9), .A7(n16_bit_adder_12_s8), .A6(n16_bit_adder_12_s7),
    .A5(n16_bit_adder_12_s6), .A4(n16_bit_adder_12_s5), .A3(n16_bit_adder_12_s4), .A2(n16_bit_adder_12_s3),
    .A1(n16_bit_adder_12_s2), .A0(n16_bit_adder_12_s1), .B15(and_224_out), .B14(and_223_out),
    .B13(and_222_out), .B12(and_221_out), .B11(and_220_out), .B10(and_219_out), .B9(and_218_out),
    .B8(and_217_out), .B7(and_216_out), .B6(and_215_out), .B5(and_214_out), .B4(and_213_out),
    .B3(and_212_out), .B2(and_211_out), .B1(and_210_out), .B0(and_209_out), .Cin(1'b0),
    .Cout(n16_bit_adder_13_cout), .S15(n16_bit_adder_13_s15), .S14(n16_bit_adder_13_s14),
    .S13(n16_bit_adder_13_s13), .S12(n16_bit_adder_13_s12), .S11(n16_bit_adder_13_s11),
    .S10(n16_bit_adder_13_s10), .S9(n16_bit_adder_13_s9), .S8(n16_bit_adder_13_s8), .S7(n16_bit_adder_13_s7),
    .S6(n16_bit_adder_13_s6), .S5(n16_bit_adder_13_s5), .S4(n16_bit_adder_13_s4), .S3(n16_bit_adder_13_s3),
    .S2(n16_bit_adder_13_s2), .S1(n16_bit_adder_13_s1), .S0(Output[13]));
  _16_bit_Adder u_16_bit_adder_14 (
    .A15(n16_bit_adder_13_cout), .A14(n16_bit_adder_13_s15), .A13(n16_bit_adder_13_s14),
    .A12(n16_bit_adder_13_s13), .A11(n16_bit_adder_13_s12), .A10(n16_bit_adder_13_s11),
    .A9(n16_bit_adder_13_s10), .A8(n16_bit_adder_13_s9), .A7(n16_bit_adder_13_s8), .A6(n16_bit_adder_13_s7),
    .A5(n16_bit_adder_13_s6), .A4(n16_bit_adder_13_s5), .A3(n16_bit_adder_13_s4), .A2(n16_bit_adder_13_s3),
    .A1(n16_bit_adder_13_s2), .A0(n16_bit_adder_13_s1), .B15(and_240_out), .B14(and_239_out),
    .B13(and_238_out), .B12(and_237_out), .B11(and_236_out), .B10(and_235_out), .B9(and_234_out),
    .B8(and_233_out), .B7(and_232_out), .B6(and_231_out), .B5(and_230_out), .B4(and_229_out),
    .B3(and_228_out), .B2(and_227_out), .B1(and_226_out), .B0(and_225_out), .Cin(1'b0),
    .Cout(n16_bit_adder_14_cout), .S15(n16_bit_adder_14_s15), .S14(n16_bit_adder_14_s14),
    .S13(n16_bit_adder_14_s13), .S12(n16_bit_adder_14_s12), .S11(n16_bit_adder_14_s11),
    .S10(n16_bit_adder_14_s10), .S9(n16_bit_adder_14_s9), .S8(n16_bit_adder_14_s8), .S7(n16_bit_adder_14_s7),
    .S6(n16_bit_adder_14_s6), .S5(n16_bit_adder_14_s5), .S4(n16_bit_adder_14_s4), .S3(n16_bit_adder_14_s3),
    .S2(n16_bit_adder_14_s2), .S1(n16_bit_adder_14_s1), .S0(Output[14]));
  _16_bit_Adder u_16_bit_adder_15 (
    .A15(n16_bit_adder_14_cout), .A14(n16_bit_adder_14_s15), .A13(n16_bit_adder_14_s14),
    .A12(n16_bit_adder_14_s13), .A11(n16_bit_adder_14_s12), .A10(n16_bit_adder_14_s11),
    .A9(n16_bit_adder_14_s10), .A8(n16_bit_adder_14_s9), .A7(n16_bit_adder_14_s8), .A6(n16_bit_adder_14_s7),
    .A5(n16_bit_adder_14_s6), .A4(n16_bit_adder_14_s5), .A3(n16_bit_adder_14_s4), .A2(n16_bit_adder_14_s3),
    .A1(n16_bit_adder_14_s2), .A0(n16_bit_adder_14_s1), .B15(and_256_out), .B14(and_255_out),
    .B13(and_254_out), .B12(and_253_out), .B11(and_252_out), .B10(and_251_out), .B9(and_250_out),
    .B8(and_249_out), .B7(and_248_out), .B6(and_247_out), .B5(and_246_out), .B4(and_245_out),
    .B3(and_244_out), .B2(and_243_out), .B1(and_242_out), .B0(and_241_out), .Cin(1'b0), .Cout(Output[31]),
    .S15(Output[30]), .S14(Output[29]), .S13(Output[28]), .S12(Output[27]), .S11(Output[26]),
    .S10(Output[25]), .S9(Output[24]), .S8(Output[23]), .S7(Output[22]), .S6(Output[21]), .S5(Output[20]),
    .S4(Output[19]), .S3(Output[18]), .S2(Output[17]), .S1(Output[16]), .S0(Output[15]));
endmodule

module _3_bit_Multiplier (
  input  A2,
  input  A1,
  input  A0,
  input  B2,
  input  B1,
  input  B0,
  input  Constant,
  output [5:0] Output,
  output Cout
);

  wire and_2_out, and_3_out, and_4_out, and_5_out, and_6_out, and_7_out, and_8_out, and_9_out,
       n4_bit_adder_1_s1, n4_bit_adder_1_s2, n4_bit_adder_1_s3;

  and and_1 (Output[0], A0, B0);
  and and_2 (and_2_out, A0, B1);
  and and_3 (and_3_out, A0, B2);
  and and_4 (and_4_out, A1, B0);
  and and_5 (and_5_out, A1, B1);
  and and_6 (and_6_out, A1, B2);
  and and_7 (and_7_out, A2, B0);
  and and_8 (and_8_out, A2, B1);
  and and_9 (and_9_out, A2, B2);
  _4_bit_Adder u_4_bit_adder_1 (
    .A3(Constant), .A2(Constant), .A1(and_3_out), .A0(and_2_out), .B3(Constant), .B2(and_6_out),
    .B1(and_5_out), .B0(and_4_out), .Cin(Constant), .S3(n4_bit_adder_1_s3), .S2(n4_bit_adder_1_s2),
    .S1(n4_bit_adder_1_s1), .S0(Output[1]));  // open: Cout
  _4_bit_Adder u_4_bit_adder_2 (
    .Cout(Cout), .A3(Constant), .A2(n4_bit_adder_1_s3), .A1(n4_bit_adder_1_s2), .A0(n4_bit_adder_1_s1),
    .B3(Constant), .B2(and_9_out), .B1(and_8_out), .B0(and_7_out), .Cin(Constant), .S3(Output[5]),
    .S2(Output[4]), .S1(Output[3]), .S0(Output[2]));
endmodule

module MiID_circuit_1 (
  input  A2,
  input  A1,
  input  A0,
  input  B2,
  input  B1,
  input  B0,
  input  Constant,
  output [5:0] Output,
  output Cout
);

  wire and_2_out, and_3_out, and_4_out, and_5_out, and_6_out, and_7_out, and_8_out, and_9_out,
       n4_bit_adder_1_s1, n4_bit_adder_1_s2, n4_bit_adder_1_s3;

  and and_1 (Output[0], A0, B0);
  and and_2 (and_2_out, A0, B1);
  and and_3 (and_3_out, A0, B2);
  and and_4 (and_4_out, A1, B0);
  and and_5 (and_5_out, A1, B1);
  and and_6 (and_6_out, A1, B2);
  and and_7 (and_7_out, A2, B0);
  and and_8 (and_8_out, A2, B1);
  and and_9 (and_9_out, A2, B2);
  _4_bit_Adder u_4_bit_adder_1 (
    .A3(Constant), .A2(Constant), .A1(and_3_out), .A0(and_2_out), .B3(Constant), .B2(and_6_out),
    .B1(and_5_out), .B0(and_4_out), .Cin(Constant), .S3(n4_bit_adder_1_s3), .S2(n4_bit_adder_1_s2),
    .S1(n4_bit_adder_1_s1), .S0(Output[1]));  // open: Cout
  _4_bit_Adder u_4_bit_adder_2 (
    .Cout(Cout), .A3(Constant), .A2(n4_bit_adder_1_s3), .A1(n4_bit_adder_1_s2), .A0(n4_bit_adder_1_s1),
    .B3(Constant), .B2(and_9_out), .B1(and_8_out), .B0(and_7_out), .Cin(Constant), .S3(Output[5]),
    .S2(Output[4]), .S1(Output[3]), .S0(Output[2]));
  // Probe on Output
endmodule

module _1_bit_ALU_for_MID (
  input  A,
  input  B,
  input  [2:0] S2S1S0,
  input  Cin,
  output Output,
  output Cout
);

  wire and_1_out, n1_bit_adder_1_s, nand_1_out, nor_1_out, not_1_out, or_1_out, xor_1_out;

  xor xor_1 (xor_1_out, A, B);
  not not_1 (not_1_out, A);
  nand nand_1 (nand_1_out, A, B);
  nor nor_1 (nor_1_out, A, B);
  or or_1 (or_1_out, A, B);
  and and_1 (and_1_out, A, B);
  _1_bit_Adder u_1_bit_adder_1 (.B(B), .Cin(Cin), .S(n1_bit_adder_1_s), .Cout(Cout), .A(A));
  Multiplexer #(.select(3), .enable("false")) multiplexer_1 (
    .in0(xor_1_out), .in1(not_1_out), .in2(nand_1_out), .in3(nor_1_out), .in4(n1_bit_adder_1_s),
    .in5(or_1_out), .in6(and_1_out), .out(Output), .sel(S2S1S0));  // open: in7
endmodule

module MID_Circuit_2__4_bit_ALU (
  input  [3:0] A,
  input  [3:0] B,
  input  [2:0] S2S1S0,
  input  Cin,
  output [3:0] Output,
  output Cout
);

  wire n1_bit_alu_for_mid_1_cout, n1_bit_alu_for_mid_2_cout, n1_bit_alu_for_mid_3_cout;

  _1_bit_ALU_for_MID u_1_bit_alu_for_mid_1 (
    .S2S1S0(S2S1S0), .Output(Output[0]), .A(A[0]), .B(B[0]), .Cin(Cin), .Cout(n1_bit_alu_for_mid_1_cout));
  _1_bit_ALU_for_MID u_1_bit_alu_for_mid_2 (
    .S2S1S0(S2S1S0), .Output(Output[1]), .A(A[1]), .B(B[1]), .Cin(n1_bit_alu_for_mid_1_cout),
    .Cout(n1_bit_alu_for_mid_2_cout));
  _1_bit_ALU_for_MID u_1_bit_alu_for_mid_3 (
    .S2S1S0(S2S1S0), .Output(Output[2]), .A(A[2]), .B(B[2]), .Cin(n1_bit_alu_for_mid_2_cout),
    .Cout(n1_bit_alu_for_mid_3_cout));
  _1_bit_ALU_for_MID u_1_bit_alu_for_mid_4 (
    .S2S1S0(S2S1S0), .Output(Output[3]), .A(A[3]), .B(B[3]), .Cin(n1_bit_alu_for_mid_3_cout), .Cout(Cout));
endmodule

module _16_bit_ALU (
  input  [1:0] Operation,
  input  [3:0] Function,
  input  [15:0] B,
  input  [15:0] A,
  input  Ainv,
  input  Binv,
  input  Sub_Cin,
  input  Add_Cin,
  output [15:0] Output,
  output Sub_Cout,
  output Add_Cout
);

  wire n4_bit_alu_1_add_cout, n4_bit_alu_1_sub_cout, n4_bit_alu_2_add_cout, n4_bit_alu_2_sub_cout,
       n4_bit_alu_3_add_cout, n4_bit_alu_3_sub_cout;

  // Probe on A
  // Probe on B
  _4_bit_ALU u_4_bit_alu_1 (
    .ALUOp(Operation), .F3F2F1F0(Function), .A3(A[3]), .A2(A[2]), .A1(A[1]), .A0(A[0]), .B3(B[3]), .B2(B[2]),
    .B1(B[1]), .B0(B[0]), .A_inv(Ainv), .B_inv(Binv), .Sub_Cin(Sub_Cin), .Add_Cin(Add_Cin), .F3(Output[3]),
    .F2(Output[2]), .F1(Output[1]), .F0(Output[0]), .Sub_Cout(n4_bit_alu_1_sub_cout),
    .Add_Cout(n4_bit_alu_1_add_cout));
  _4_bit_ALU u_4_bit_alu_2 (
    .ALUOp(Operation), .F3F2F1F0(Function), .A3(A[7]), .A2(A[6]), .A1(A[5]), .A0(A[4]), .B3(B[7]), .B2(B[6]),
    .B1(B[5]), .B0(B[4]), .A_inv(Ainv), .B_inv(Binv), .Sub_Cin(n4_bit_alu_1_sub_cout),
    .Add_Cin(n4_bit_alu_1_add_cout), .F3(Output[7]), .F2(Output[6]), .F1(Output[5]), .F0(Output[4]),
    .Sub_Cout(n4_bit_alu_2_sub_cout), .Add_Cout(n4_bit_alu_2_add_cout));
  _4_bit_ALU u_4_bit_alu_3 (
    .ALUOp(Operation), .F3F2F1F0(Function), .A3(A[11]), .A2(A[10]), .A1(A[9]), .A0(A[8]), .B3(B[11]),
    .B2(B[10]), .B1(B[9]), .B0(B[8]), .A_inv(Ainv), .B_inv(Binv), .Sub_Cin(n4_bit_alu_2_sub_cout),
    .Add_Cin(n4_bit_alu_2_add_cout), .F3(Output[11]), .F2(Output[10]), .F1(Output[9]), .F0(Output[8]),
    .Sub_Cout(n4_bit_alu_3_sub_cout), .Add_Cout(n4_bit_alu_3_add_cout));
  _4_bit_ALU u_4_bit_alu_4 (
    .ALUOp(Operation), .F3F2F1F0(Function), .A3(A[15]), .A2(A[14]), .A1(A[13]), .A0(A[12]), .B3(B[15]),
    .B2(B[14]), .B1(B[13]), .B0(B[12]), .A_inv(Ainv), .B_inv(Binv), .Sub_Cin(n4_bit_alu_3_sub_cout),
    .Add_Cin(n4_bit_alu_3_add_cout), .F3(Output[15]), .F2(Output[14]), .F1(Output[13]), .F0(Output[12]),
    .Sub_Cout(Sub_Cout), .Add_Cout(Add_Cout));
  // Probe on Output
endmodule

module Register_File (
  input  Write_En,
  input  [3:0] RS,
  input  [3:0] RD,
  input  Clock,
  input  [3:0] RT,
  input  Reset,
  input  [15:0] Data,
  output [15:0] Data_1,
  output [15:0] Data_2
);

  wire demultiplexer_1_out0, demultiplexer_1_out1, demultiplexer_1_out2, demultiplexer_1_out3,
       demultiplexer_1_out4, demultiplexer_1_out5, demultiplexer_1_out6, demultiplexer_1_out7,
       demultiplexer_1_out8, demultiplexer_1_out9, demultiplexer_1_out10, demultiplexer_1_out11,
       demultiplexer_1_out12, demultiplexer_1_out13, demultiplexer_1_out14, demultiplexer_1_out15;
  wire [15:0] _00_q, _01_q, _02_q, _03_q, _04_q, _05_q, _06_q, _07_q, _08_q, _09_q, _10_q, _11_q, _12_q,
       _13_q, _14_q, _15_q;

  Demultiplexer #(.select(4), .enable("false")) demultiplexer_1 (
    .out0(demultiplexer_1_out0), .out1(demultiplexer_1_out1), .out2(demultiplexer_1_out2),
    .out3(demultiplexer_1_out3), .out4(demultiplexer_1_out4), .out5(demultiplexer_1_out5),
    .out6(demultiplexer_1_out6), .out7(demultiplexer_1_out7), .out8(demultiplexer_1_out8),
    .out9(demultiplexer_1_out9), .out10(demultiplexer_1_out10), .out11(demultiplexer_1_out11),
    .out12(demultiplexer_1_out12), .out13(demultiplexer_1_out13), .out14(demultiplexer_1_out14),
    .out15(demultiplexer_1_out15), .in(Write_En), .sel(RD));
  Register #(.width(16)) _00 (.D(Data), .en(demultiplexer_1_out0), .Q(_00_q), .clk(Clock), .clr(Reset));
  Register #(.width(16)) _01 (.D(Data), .en(demultiplexer_1_out1), .Q(_01_q), .clk(Clock), .clr(Reset));
  Register #(.width(16)) _02 (.D(Data), .en(demultiplexer_1_out2), .Q(_02_q), .clk(Clock), .clr(Reset));
  Register #(.width(16)) _03 (.D(Data), .en(demultiplexer_1_out3), .Q(_03_q), .clk(Clock), .clr(Reset));
  Register #(.width(16)) _04 (.D(Data), .en(demultiplexer_1_out4), .Q(_04_q), .clk(Clock), .clr(Reset));
  Register #(.width(16)) _05 (.D(Data), .en(demultiplexer_1_out5), .Q(_05_q), .clk(Clock), .clr(Reset));
  Register #(.width(16)) _06 (.D(Data), .en(demultiplexer_1_out6), .Q(_06_q), .clk(Clock), .clr(Reset));
  Register #(.width(16)) _07 (.D(Data), .en(demultiplexer_1_out7), .Q(_07_q), .clk(Clock), .clr(Reset));
  Register #(.width(16)) _08 (.D(Data), .en(demultiplexer_1_out8), .Q(_08_q), .clk(Clock), .clr(Reset));
  Register #(.width(16)) _09 (.D(Data), .en(demultiplexer_1_out9), .Q(_09_q), .clk(Clock), .clr(Reset));
  Register #(.width(16)) _10 (.D(Data), .en(demultiplexer_1_out10), .Q(_10_q), .clk(Clock), .clr(Reset));
  Register #(.width(16)) _11 (.D(Data), .en(demultiplexer_1_out11), .Q(_11_q), .clk(Clock), .clr(Reset));
  Register #(.width(16)) _12 (.D(Data), .en(demultiplexer_1_out12), .Q(_12_q), .clk(Clock), .clr(Reset));
  Register #(.width(16)) _13 (.D(Data), .en(demultiplexer_1_out13), .Q(_13_q), .clk(Clock), .clr(Reset));
  Register #(.width(16)) _14 (.D(Data), .en(demultiplexer_1_out14), .Q(_14_q), .clk(Clock), .clr(Reset));
  Register #(.width(16)) _15 (.D(Data), .en(demultiplexer_1_out15), .Q(_15_q), .clk(Clock), .clr(Reset));
  // Probe on Data_1
  Multiplexer #(.select(4), .width(16), .enable("false")) multiplexer_1 (
    .in0(_00_q), .in1(_01_q), .in2(_02_q), .in3(_03_q), .in4(_04_q), .in5(_05_q), .in6(_06_q), .in7(_07_q),
    .in8(_08_q), .in9(_09_q), .in10(_10_q), .in11(_11_q), .in12(_12_q), .in13(_13_q), .in14(_14_q),
    .in15(_15_q), .out(Data_1), .sel(RS));
  // Probe on Data_2
  Multiplexer #(.select(4), .width(16), .enable("false")) multiplexer_2 (
    .in0(_00_q), .in1(_01_q), .in2(_02_q), .in3(_03_q), .in4(_04_q), .in5(_05_q), .in6(_06_q), .in7(_07_q),
    .in8(_08_q), .in9(_09_q), .in10(_10_q), .in11(_11_q), .in12(_12_q), .in13(_13_q), .in14(_14_q),
    .in15(_15_q), .out(Data_2), .sel(RT));
endmodule

module R_Type_Data_Path (
  input  Ainv,
  input  Sub_Cin,
  input  Binv,
  input  Add_Cin,
  input  [1:0] ALUOp,
  input  [3:0] Function,
  input  R_write,
  input  Reset,
  output [3:0] OP,
  output [3:0] RS,
  output [3:0] RT,
  output [3:0] RD,
  output Add_Cout,
  output Sub_Cout
);

  wire Clock_out;
  wire [15:0] adder_1_out, n16_bit_alu_1_output, register_1_q, register_file_1_data_1, register_file_1_data_2;

  Register #(.width(16)) register_1 (.D(adder_1_out), .Q(register_1_q), .clk(Clock_out));  // open: en, clr
  Adder #(.width(16)) adder_1 (.a(register_1_q), .b(16'h1), .out(adder_1_out));  // open: cin, cout
  Clock Clock (.out(Clock_out));
  ROM #(.addrWidth(16), .dataWidth(16)) rom_1 (.addr(register_1_q), .data({OP, RS, RT, RD}));  // open: sel
  // Probe on register_file_1_data_1
  Register_File register_file_1 (
    .Write_En(R_write), .RD(RD), .Clock(Clock_out), .Reset(Reset), .Data(n16_bit_alu_1_output),
    .Data_1(register_file_1_data_1), .RS(RS), .Data_2(register_file_1_data_2), .RT(RT));
  // Probe on register_file_1_data_2
  // Probe on n16_bit_alu_1_output
  _16_bit_ALU u_16_bit_alu_1 (
    .A(register_file_1_data_1), .B(register_file_1_data_2), .Operation(ALUOp), .Function(Function),
    .Ainv(Ainv), .Binv(Binv), .Sub_Cin(Sub_Cin), .Add_Cin(Add_Cin), .Sub_Cout(Sub_Cout), .Add_Cout(Add_Cout),
    .Output(n16_bit_alu_1_output));

  // Notes on the sheet:
  //   contents of rom_1 (hex, n*v repeats v):
  //   123
endmodule

module I_type_data_path (
  input  Ainv,
  input  Binv,
  input  Sub_Cin,
  input  Add_Cin,
  input  [1:0] ALUOp,
  input  [3:0] Function,
  input  R_write,
  input  Reset,
  output [3:0] OP,
  output [15:0] Data_1,
  output [3:0] RS,
  output [15:0] IMM,
  output [3:0] RT__Destination,
  output [3:0] Imm_2,
  output Sub_Cout,
  output Add_Cout
);

  wire Clock_out;
  wire [15:0] adder_1_out, n16_bit_alu_1_output, register_1_q;

  Register #(.width(16)) register_1 (.D(adder_1_out), .Q(register_1_q), .clk(Clock_out));  // open: en, clr
  Clock Clock (.out(Clock_out));
  Adder #(.width(16)) adder_1 (.a(register_1_q), .b(16'h1), .out(adder_1_out));  // open: cin, cout
  ROM #(.addrWidth(16), .dataWidth(16)) rom_1 (
    .addr(register_1_q), .data({OP, RS, RT__Destination, Imm_2}));  // open: sel
  assign IMM = {{12{1'b0}}, Imm_2};  // Bit_Extender bit_extender_1
  Register_File register_file_1 (
    .Write_En(R_write), .RD(RT__Destination), .Clock(Clock_out), .Reset(Reset), .Data(n16_bit_alu_1_output),
    .Data_1(Data_1), .RS(RS));  // open: Data_2, RT
  _16_bit_ALU u_16_bit_alu_1 (
    .A(Data_1), .B(IMM), .Operation(ALUOp), .Function(Function), .Ainv(Ainv), .Binv(Binv), .Sub_Cin(Sub_Cin),
    .Add_Cin(Add_Cin), .Sub_Cout(Sub_Cout), .Add_Cout(Add_Cout), .Output(n16_bit_alu_1_output));
  // Probe on n16_bit_alu_1_output

  // Notes on the sheet:
  //   addi $r4, $r2, 5
  //   After writing $r4 will be assigned with
  //   $r2 = 7
  //   hexadecimal value c.
  //   contents of rom_1 (hex, n*v repeats v):
  //   245
endmodule

module Load_and_Store (
  input  Ainv,
  input  Binv,
  input  Sub_Cin,
  input  Add_Cin,
  input  Store,
  input  Load,
  input  [1:0] ALUOp,
  input  [3:0] Function,
  input  R_write,
  input  Reset,
  output [15:0] Data_1,
  output [3:0] OP,
  output [15:0] Data_2,
  output [3:0] RS,
  output [3:0] RT__Destination,
  output [3:0] RD,
  output [15:0] Effective_Address,
  output Sub_Cout,
  output Add_Cout
);

  wire Clock_out;
  wire [15:0] adder_1_out, bit_extender_1_out, ram_1_data, register_1_q;

  Register #(.width(16)) register_1 (.D(adder_1_out), .Q(register_1_q), .clk(Clock_out));  // open: en, clr
  Clock Clock (.out(Clock_out));
  Adder #(.width(16)) adder_1 (.a(register_1_q), .b(16'h1), .out(adder_1_out));  // open: cin, cout
  ROM #(.addrWidth(16), .dataWidth(16)) rom_1 (.addr(register_1_q), .data({OP, RS, RT__Destination, RD}));  // open: sel
  assign bit_extender_1_out = {{12{1'b0}}, RD};  // Bit_Extender bit_extender_1
  Register_File register_file_1 (
    .Write_En(R_write), .RD(RT__Destination), .Clock(Clock_out), .Reset(Reset), .Data(ram_1_data),
    .Data_1(Data_1), .RS(RS), .Data_2(Data_2), .RT(RT__Destination));
  _16_bit_ALU u_16_bit_alu_1 (
    .A(Data_1), .B(bit_extender_1_out), .Operation(ALUOp), .Function(Function), .Ainv(Ainv), .Binv(Binv),
    .Sub_Cin(Sub_Cin), .Add_Cin(Add_Cin), .Sub_Cout(Sub_Cout), .Add_Cout(Add_Cout), .Output(Effective_Address));
  RAM #(.addrWidth(16), .dataWidth(16), .bus("separate")) ram_1 (
    .addr(Effective_Address), .din(Data_2), .data(ram_1_data), .str(Store), .clk(Clock_out), .ld(Load));  // open: sel, clr

  // Notes on the sheet:
  //   contents of rom_1 (hex, n*v repeats v):
  //   123
endmodule

module Data_Path (
  input  Reset,
  output [3:0] OP,
  output [3:0] RS,
  output [3:0] RT__Destination,
  output [15:0] Effective_Address,
  output [3:0] RD,
  output Sub_Cout,
  output Add_Cout
);

  wire Ainv, ALU___Memory, Binv, Cin, Clock, LW, R_dest, R_type___I_type, R_write, SW;
  wire [1:0] ALUOp;
  wire [3:0] Function, multiplexer_1_out;
  wire [15:0] adder_1_out, bit_extender_1_out, Data, multiplexer_2_out, ram_1_data, register_1_q,
       register_file_1_data_1, register_file_1_data_2;

  Register #(.width(16)) register_1 (.D(adder_1_out), .Q(register_1_q), .clk(Clock), .clr(Reset));  // open: en
  Clock u_Clock (.out(Clock));
  Adder #(.width(16)) adder_1 (.a(register_1_q), .b(16'h1), .out(adder_1_out));  // open: cin, cout
  ROM #(.addrWidth(16), .dataWidth(16)) rom_1 (.addr(register_1_q), .data({OP, RS, RT__Destination, RD}), .sel(1'b1));
  Multiplexer #(.width(4), .enable("false")) multiplexer_1 (
    .in0(RT__Destination), .in1(RD), .out(multiplexer_1_out), .sel(R_dest));
  assign bit_extender_1_out = {{12{1'b0}}, RD};  // Bit_Extender bit_extender_1
  Register_File register_file_1 (
    .Write_En(R_write), .RD(multiplexer_1_out), .Clock(Clock), .Reset(Reset), .Data(Data),
    .Data_1(register_file_1_data_1), .RS(RS), .Data_2(register_file_1_data_2), .RT(RT__Destination));
  Main_Control_Unit main_control_unit_1 (
    .in_1(OP), .R_dest(R_dest), .R_type___I_type(R_type___I_type), .ALU___Memory(ALU___Memory),
    .R_write(R_write), .SW(SW), .LW(LW), .ALUOp(ALUOp), .Function(Function), .Cin(Cin), .Ainv(Ainv),
    .Binv(Binv));
  Multiplexer #(.width(16), .enable("false")) multiplexer_2 (
    .in0(register_file_1_data_2), .in1(bit_extender_1_out), .out(multiplexer_2_out), .sel(R_type___I_type));
  _16_bit_ALU u_16_bit_alu_1 (
    .A(register_file_1_data_1), .B(multiplexer_2_out), .Operation(ALUOp), .Function(Function), .Ainv(Ainv),
    .Binv(Binv), .Sub_Cin(Cin), .Add_Cin(Cin), .Sub_Cout(Sub_Cout), .Add_Cout(Add_Cout),
    .Output(Effective_Address));
  RAM #(.addrWidth(16), .dataWidth(16), .bus("separate")) ram_1 (
    .addr(Effective_Address), .din(register_file_1_data_2), .data(ram_1_data), .str(SW), .clk(Clock),
    .ld(LW), .clr(Reset));  // open: sel
  Multiplexer #(.width(16), .enable("false")) multiplexer_3 (
    .in0(Effective_Address), .in1(ram_1_data), .out(Data), .sel(ALU___Memory));

  // Other names for the same wires on the sheet: Opcode[3:0] = OP

  // Notes on the sheet:
  //   contents of rom_1 (hex, n*v repeats v):
  //   4123
endmodule

module Main_Control_Unit (
  input  [3:0] in_1,
  output R_dest,
  output R_type___I_type,
  output ALU___Memory,
  output R_write,
  output SW,
  output LW,
  output [1:0] ALUOp,
  output [3:0] Function,
  output Cin,
  output Ainv,
  output Binv
);

  wire and_2_out, and_3_out, and_4_out, and_5_out, and_6_out, not_2_out, not_3_out, not_4_out, not_5_out;

  not not_1 (Ainv, 1'b1);
  not not_2 (not_2_out, in_1[3]);
  not not_3 (not_3_out, in_1[2]);
  not not_4 (not_4_out, in_1[1]);
  not not_5 (not_5_out, in_1[0]);
  and and_1 (Function[0], not_2_out, in_1[2], in_1[1], in_1[0]);
  and and_2 (and_2_out, not_2_out, in_1[2], in_1[1], not_5_out);
  and and_3 (and_3_out, not_2_out, not_3_out, not_4_out, not_5_out);
  and and_4 (and_4_out, not_2_out, not_3_out, in_1[1], not_5_out);
  and and_5 (and_5_out, not_2_out, not_3_out, not_4_out, in_1[0]);
  and and_6 (and_6_out, not_2_out, not_3_out, in_1[1], in_1[0]);
  and and_7 (SW, in_1[3], in_1[2], in_1[1], not_5_out);
  and and_8 (ALU___Memory, not_2_out, in_1[2], not_4_out, not_5_out);
  or or_1 (Binv, and_4_out, and_6_out);
  or or_2 (Function[2], and_2_out, Function[0]);
  or or_3 (R_dest, and_2_out, Function[0], and_3_out, and_4_out);
  or or_4 (R_type___I_type, and_5_out, and_6_out, SW, ALU___Memory);
  or or_5 (R_write, and_2_out, Function[0], and_3_out, and_4_out, and_5_out, and_6_out, ALU___Memory);

  assign ALUOp = {1'b1, Ainv};
  assign Cin = Binv;
  assign {Function[3], Function[1]} = {Ainv, Binv};
  assign LW = ALU___Memory;
endmodule
